// Logisim project ClassicalCPU.circ as structural Verilog: 16 circuits, main circuit main
module main (
  input  _0,
  input  _1,
  input  _2,
  input  _3,
  input  _4,
  input  _5,
  input  _6,
  input  _7,
  input  _8,
  input  _9,
  input  in_11
);

  wire _1_out, _2_out, _4_out, _8_out, _16_out, _32_out, _64_out, _128_out, ALU_out_26, ALU_out_27,
       ALU_out_28, ALU_out_29, ALU_out_30, ALU_out_31, ALU_out_32, ALU_out_33, ALU_out_34, ALU_to_cu,
       ALU_zero, and_1_out, and_2_out, and_3_out, and_4_out, and_5_out, and_6_out,
       bus_cpu_system_gate_1_out_11, bus_cpu_system_gate_1_out_12, bus_cpu_system_gate_1_out_13,
       bus_cpu_system_gate_1_out_14, bus_cpu_system_gate_1_out_15, bus_cpu_system_gate_1_out_16,
       bus_cpu_system_gate_1_out_17, bus_cpu_system_gate_1_out_18, bus_cpu_system_gate_1_out_19,
       bus_cpu_system_gate_1_out_20, bus_cpu_system_gate_1_out_21, bus_cpu_system_gate_1_out_22,
       bus_cpu_system_gate_1_out_23, bus_cpu_system_gate_1_out_24, bus_cpu_system_gate_1_out_25,
       bus_cpu_system_gate_1_out_26, bus_gate_1_out_17, bus_gate_1_out_18, bus_gate_1_out_19,
       bus_gate_1_out_20, bus_gate_1_out_21, bus_gate_1_out_22, bus_gate_1_out_23, bus_gate_1_out_24,
       bus_gate_2_out_17, bus_gate_2_out_18, bus_gate_2_out_19, bus_gate_2_out_20, bus_gate_2_out_21,
       bus_gate_2_out_22, bus_gate_2_out_23, bus_gate_2_out_24, bus_gate_3_out_17, bus_gate_3_out_18,
       bus_gate_3_out_19, bus_gate_3_out_20, bus_gate_3_out_21, bus_gate_3_out_22, bus_gate_3_out_23,
       bus_gate_3_out_24, bus_gate_4_out_17, bus_gate_4_out_18, bus_gate_4_out_19, bus_gate_4_out_20,
       bus_gate_4_out_21, bus_gate_4_out_22, bus_gate_4_out_23, bus_gate_4_out_24, bus_gate_5_out_17,
       bus_gate_5_out_18, bus_gate_5_out_19, bus_gate_5_out_20, bus_gate_5_out_21, bus_gate_5_out_22,
       bus_gate_5_out_23, bus_gate_5_out_24, bus_gate_6_out_17, bus_gate_6_out_18, bus_gate_6_out_19,
       bus_gate_6_out_20, bus_gate_6_out_21, bus_gate_6_out_22, bus_gate_6_out_23, bus_gate_6_out_24,
       button_1_out, button_2_out, CLK_bz_end, CLK_clk, CLK_on_off, CLK_out_9, CLK_out_10, CLK_out_11,
       CLK_out_12, CLK_out_13, CLK_out_14, CLK_out_15, CLK_reset, display_buffer_out_12,
       display_buffer_out_13, display_buffer_out_14, display_buffer_out_15, display_buffer_out_16,
       display_buffer_out_17, display_buffer_out_18, display_buffer_out_19, display_buffer_out_20,
       display_buffer_out_21, display_buffer_out_22, display_buffer_out_23, display_buffer_out_24,
       display_buffer_out_25, GR0_out_21, GR0_out_22, GR0_out_23, GR0_out_24, GR0_out_25, GR0_out_26,
       GR0_out_27, GR0_out_28, GR1_out_21, GR1_out_22, GR1_out_23, GR1_out_24, GR1_out_25, GR1_out_26,
       GR1_out_27, GR1_out_28, Inputer_buffer_out_14, Inputer_buffer_out_15, Inputer_buffer_out_16,
       Inputer_buffer_out_17, IR_address, IR_adress, IR_alu_cu, IR_alu_r_r_w, IR_bz, IR_halt, IR_inp, IR_l_r,
       IR_mar_mbr_r_w, IR_n_l, IR_out_18, IR_out_19, IR_out_20, IR_out_36, IR_out_38, IR_out_39, IR_out_40,
       IR_prt, IR_r_w, IR_ram_r_w, IR_reset_alu, IR_reset_mbr, IR_tick, IR_to_ram, mar_mbr_1_out_27,
       mar_mbr_1_out_28, mar_mbr_1_out_29, mar_mbr_1_out_30, mar_mbr_1_out_31, mar_mbr_1_out_32,
       mar_mbr_1_out_33, mar_mbr_1_out_34, mar_mbr_1_out_35, mar_mbr_1_out_36, mar_mbr_1_out_37,
       mar_mbr_1_out_38, not_1_out, not_2_out, not_3_out, ON_out, or_1_out, or_2_out, pc_1_out_13,
       pc_1_out_15, pc_1_out_16, pc_1_to_mar, RAM_out_28, RAM_out_29, RAM_out_30, RAM_out_31, RAM_out_32,
       RAM_out_33, RAM_out_34, RAM_out_35, RAM_out_36;

  Button ON (.out(ON_out));
  clock CLK (
    .Input_form_CU(IR_out_20), .out_13(CLK_out_13), .out_14(CLK_out_14), .CLK(CLK_clk),
    .Button_ON_OFF(ON_out), .HALT(IR_halt), .out_12(CLK_out_12), .out_15(CLK_out_15), .out_9(CLK_out_9),
    .out_11(CLK_out_11), .BZ(IR_bz), .BZ_end(CLK_bz_end), .ON_OFF(CLK_on_off), .out_10(CLK_out_10),
    .Reset(CLK_reset));
  IR IR (
    .CLK(CLK_clk), .in_2(CLK_out_10), .RESET(CLK_reset), .in_6(bus_gate_1_out_24), .in_7(bus_gate_1_out_23),
    .in_8(bus_gate_1_out_22), .in_9(bus_gate_1_out_21), .in_10(bus_gate_1_out_20), .in_11(bus_gate_1_out_19),
    .in_12(bus_gate_1_out_18), .in_13(bus_gate_1_out_17), .in_14(CLK_on_off), .out_36(IR_out_36),
    .adress(IR_adress), .out_39(IR_out_39), .out_40(IR_out_40), .Tick(IR_tick), .ALU_back(ALU_out_26),
    .ALU_R_R_W(IR_alu_r_r_w), .out_38(IR_out_38), .in_16(ALU_to_cu), .ALU_CU(IR_alu_cu), .L_R(IR_l_r),
    .reset_ALU(IR_reset_alu), .N_L(IR_n_l), .RAM_R_W(IR_ram_r_w), .R_W(IR_r_w), .ADDRESS(IR_address),
    .out_18(IR_out_18), .out_19(IR_out_19), .ZERO(ALU_zero), .BZ(IR_bz), .out_20(IR_out_20),
    .BZ_done(CLK_bz_end), .MAR_MBR_R_W(IR_mar_mbr_r_w), .reset_MBR(IR_reset_mbr), .to_RAM(IR_to_ram),
    .from_RAM(RAM_out_28), .INP(IR_inp), .PRT(IR_prt), .HALT(IR_halt));
  not not_1 (not_1_out, IR_l_r);
  not not_2 (not_2_out, IR_alu_r_r_w);
  PC pc_1 (
    .CLK(CLK_out_13), .in_2(CLK_out_12), .ON(CLK_reset), .in_4(IR_out_36), .BZ(IR_adress), .in_6(IR_out_39),
    .in_7(IR_out_40), .in_8(IR_bz), .CLK_2(CLK_on_off), .in_10(CLK_out_14), .out_13(pc_1_out_13),
    .to_MAR(pc_1_to_mar), .out_15(pc_1_out_15), .out_16(pc_1_out_16), .in_11(CLK_out_13), .Reset(ON_out));
  and and_1 (and_1_out, not_1_out, IR_alu_r_r_w);
  and and_2 (and_2_out, IR_l_r, not_2_out);
  not not_3 (not_3_out, IR_out_38);
  or or_1 (or_1_out, CLK_reset, IR_out_20, CLK_out_9);
  BUS_gate bus_gate_1 (
    .in_1(bus_gate_2_out_24), .in_2(bus_gate_5_out_17), .in_3(bus_gate_2_out_23), .in_4(bus_gate_5_out_18),
    .in_5(bus_gate_2_out_22), .in_6(bus_gate_5_out_19), .in_7(bus_gate_2_out_21), .in_8(bus_gate_5_out_20),
    .in_9(bus_gate_2_out_20), .in_10(bus_gate_5_out_21), .in_11(bus_gate_2_out_19),
    .in_12(bus_gate_5_out_22), .in_13(bus_gate_2_out_18), .in_14(bus_gate_5_out_23),
    .in_15(bus_gate_2_out_17), .in_16(bus_gate_5_out_24), .out_17(bus_gate_1_out_17),
    .out_18(bus_gate_1_out_18), .out_19(bus_gate_1_out_19), .out_20(bus_gate_1_out_20),
    .out_21(bus_gate_1_out_21), .out_22(bus_gate_1_out_22), .out_23(bus_gate_1_out_23),
    .out_24(bus_gate_1_out_24));
  or or_2 (or_2_out, IR_reset_alu, CLK_reset);
  and and_3 (and_3_out, IR_address, IR_out_38);
  and and_4 (and_4_out, IR_address, not_3_out);
  MAR___MBR mar_mbr_1 (
    .in_2(IR_tick), .Reset(CLK_reset), .in_5(CLK_out_14), .in_12(CLK_on_off), .in_14(CLK_out_15),
    .CLK_2(CLK_out_10), .in_17(bus_gate_1_out_24), .in_18(bus_gate_1_out_23), .in_19(bus_gate_1_out_22),
    .in_20(bus_gate_1_out_21), .in_21(bus_gate_1_out_20), .in_22(bus_gate_1_out_19),
    .in_23(bus_gate_1_out_18), .in_24(bus_gate_1_out_17), .in_25(IR_out_18), .in_26(CLK_out_11),
    .out_27(mar_mbr_1_out_27), .out_28(mar_mbr_1_out_28), .out_29(mar_mbr_1_out_29),
    .out_30(mar_mbr_1_out_30), .out_31(mar_mbr_1_out_31), .out_32(mar_mbr_1_out_32),
    .out_33(mar_mbr_1_out_33), .out_34(mar_mbr_1_out_34), .out_35(mar_mbr_1_out_35),
    .out_36(mar_mbr_1_out_36), .out_37(mar_mbr_1_out_37), .out_38(mar_mbr_1_out_38), .CLK(pc_1_out_13),
    .in_6(pc_1_to_mar), .in_7(pc_1_out_15), .in_8(pc_1_out_16), .in_9(IR_out_36), .in_10(IR_adress),
    .in_11(IR_out_39), .in_13(IR_out_40), .CU_LD(IR_mar_mbr_r_w), .Reset_MBR(IR_reset_mbr));
  ALU__8_bit ALU (
    .Zero(ALU_zero), .R_negative(in_11), .L_negative(IR_n_l), .in_5(bus_gate_2_out_17),
    .in_6(bus_gate_2_out_18), .in_7(bus_gate_2_out_19), .in_8(bus_gate_2_out_20), .in_9(bus_gate_2_out_21),
    .in_10(bus_gate_2_out_22), .in_11(bus_gate_2_out_23), .in_12(bus_gate_2_out_24),
    .in_14(bus_gate_2_out_17), .in_15(bus_gate_2_out_18), .in_16(bus_gate_2_out_19),
    .in_17(bus_gate_2_out_20), .in_18(bus_gate_2_out_21), .in_19(bus_gate_2_out_22),
    .in_20(bus_gate_2_out_23), .in_21(bus_gate_2_out_24), .out_27(ALU_out_27), .out_28(ALU_out_28),
    .out_29(ALU_out_29), .out_30(ALU_out_30), .out_31(ALU_out_31), .out_32(ALU_out_32), .out_33(ALU_out_33),
    .out_34(ALU_out_34), .ON_OFF(CLK_on_off), .Clock(CLK_clk), .in_2(IR_alu_cu), .in_13(and_1_out),
    .in_22(and_2_out), .out_26(ALU_out_26), .to_CU(ALU_to_cu), .in_4(or_2_out));  // open: Status, Negative
  register__8_bit GR1 (
    .in_6(bus_gate_2_out_17), .in_7(bus_gate_2_out_18), .in_8(bus_gate_2_out_19), .in_9(bus_gate_2_out_20),
    .in_10(bus_gate_2_out_21), .in_11(bus_gate_2_out_22), .in_12(bus_gate_2_out_23),
    .in_13(bus_gate_2_out_24), .out_21(GR1_out_21), .out_22(GR1_out_22), .out_23(GR1_out_23),
    .out_24(GR1_out_24), .out_25(GR1_out_25), .out_26(GR1_out_26), .out_27(GR1_out_27), .out_28(GR1_out_28),
    .in_1(IR_tick), .W_R(and_5_out), .Address(and_3_out), .RESET(CLK_reset));  // open: in_2, in_3, in_4, in_5, in_14, in_15, in_16, in_17
  and and_5 (and_5_out, IR_out_38, IR_r_w);
  register__8_bit GR0 (
    .in_6(bus_gate_2_out_17), .in_7(bus_gate_2_out_18), .in_8(bus_gate_2_out_19), .in_9(bus_gate_2_out_20),
    .in_10(bus_gate_2_out_21), .in_11(bus_gate_2_out_22), .in_12(bus_gate_2_out_23),
    .in_13(bus_gate_2_out_24), .out_21(GR0_out_21), .out_22(GR0_out_22), .out_23(GR0_out_23),
    .out_24(GR0_out_24), .out_25(GR0_out_25), .out_26(GR0_out_26), .out_27(GR0_out_27), .out_28(GR0_out_28),
    .in_1(IR_tick), .W_R(and_6_out), .Address(and_4_out), .RESET(CLK_reset));  // open: in_2, in_3, in_4, in_5, in_14, in_15, in_16, in_17
  and and_6 (and_6_out, not_3_out, IR_r_w);
  BUS_CPU_System_gate bus_cpu_system_gate_1 (
    .in_10(IR_out_19), .out_11(bus_cpu_system_gate_1_out_11), .out_19(bus_cpu_system_gate_1_out_19),
    .out_12(bus_cpu_system_gate_1_out_12), .out_20(bus_cpu_system_gate_1_out_20),
    .out_13(bus_cpu_system_gate_1_out_13), .out_21(bus_cpu_system_gate_1_out_21),
    .out_14(bus_cpu_system_gate_1_out_14), .out_22(bus_cpu_system_gate_1_out_22),
    .out_15(bus_cpu_system_gate_1_out_15), .out_23(bus_cpu_system_gate_1_out_23),
    .out_16(bus_cpu_system_gate_1_out_16), .out_24(bus_cpu_system_gate_1_out_24),
    .out_17(bus_cpu_system_gate_1_out_17), .out_25(bus_cpu_system_gate_1_out_25),
    .out_18(bus_cpu_system_gate_1_out_18), .out_26(bus_cpu_system_gate_1_out_26), .in_1(mar_mbr_1_out_38),
    .ON(CLK_on_off), .in_2(mar_mbr_1_out_37), .in_3(mar_mbr_1_out_36), .in_4(mar_mbr_1_out_35),
    .in_5(mar_mbr_1_out_34), .in_6(mar_mbr_1_out_33), .in_7(mar_mbr_1_out_32), .in_8(mar_mbr_1_out_31));
  BUS_gate bus_gate_2 (
    .in_1(bus_cpu_system_gate_1_out_18), .in_2(bus_gate_3_out_17), .in_3(bus_cpu_system_gate_1_out_17),
    .in_4(bus_gate_3_out_18), .in_5(bus_cpu_system_gate_1_out_16), .in_6(bus_gate_3_out_19),
    .in_7(bus_cpu_system_gate_1_out_15), .in_8(bus_gate_3_out_20), .in_9(bus_cpu_system_gate_1_out_14),
    .in_10(bus_gate_3_out_21), .in_11(bus_cpu_system_gate_1_out_13), .in_12(bus_gate_3_out_22),
    .in_13(bus_cpu_system_gate_1_out_12), .in_14(bus_gate_3_out_23), .in_15(bus_cpu_system_gate_1_out_11),
    .in_16(bus_gate_3_out_24), .out_17(bus_gate_2_out_17), .out_18(bus_gate_2_out_18),
    .out_19(bus_gate_2_out_19), .out_20(bus_gate_2_out_20), .out_21(bus_gate_2_out_21),
    .out_22(bus_gate_2_out_22), .out_23(bus_gate_2_out_23), .out_24(bus_gate_2_out_24));
  BUS_gate bus_gate_3 (
    .in_1(bus_gate_4_out_17), .in_2(ALU_out_27), .in_3(bus_gate_4_out_18), .in_4(ALU_out_28),
    .in_5(bus_gate_4_out_19), .in_6(ALU_out_29), .in_7(bus_gate_4_out_20), .in_8(ALU_out_30),
    .in_9(bus_gate_4_out_21), .in_10(ALU_out_31), .in_11(bus_gate_4_out_22), .in_12(ALU_out_32),
    .in_13(bus_gate_4_out_23), .in_14(ALU_out_33), .in_15(bus_gate_4_out_24), .in_16(ALU_out_34),
    .out_17(bus_gate_3_out_17), .out_18(bus_gate_3_out_18), .out_19(bus_gate_3_out_19),
    .out_20(bus_gate_3_out_20), .out_21(bus_gate_3_out_21), .out_22(bus_gate_3_out_22),
    .out_23(bus_gate_3_out_23), .out_24(bus_gate_3_out_24));
  BUS_gate bus_gate_4 (
    .in_1(GR0_out_21), .in_2(GR1_out_21), .in_3(GR0_out_22), .in_4(GR1_out_22), .in_5(GR0_out_23),
    .in_6(GR1_out_23), .in_7(GR0_out_24), .in_8(GR1_out_24), .in_9(GR0_out_25), .in_10(GR1_out_25),
    .in_11(GR0_out_26), .in_12(GR1_out_26), .in_13(GR0_out_27), .in_14(GR1_out_27), .in_15(GR0_out_28),
    .in_16(GR1_out_28), .out_17(bus_gate_4_out_17), .out_18(bus_gate_4_out_18), .out_19(bus_gate_4_out_19),
    .out_20(bus_gate_4_out_20), .out_21(bus_gate_4_out_21), .out_22(bus_gate_4_out_22),
    .out_23(bus_gate_4_out_23), .out_24(bus_gate_4_out_24));
  BUS_gate bus_gate_5 (
    .in_1(bus_cpu_system_gate_1_out_19), .in_2(bus_gate_6_out_17), .in_3(bus_cpu_system_gate_1_out_20),
    .in_4(bus_gate_6_out_18), .in_5(bus_cpu_system_gate_1_out_21), .in_6(bus_gate_6_out_19),
    .in_7(bus_cpu_system_gate_1_out_22), .in_8(bus_gate_6_out_20), .in_9(bus_cpu_system_gate_1_out_23),
    .in_10(bus_gate_6_out_21), .in_11(bus_cpu_system_gate_1_out_24), .in_12(bus_gate_6_out_22),
    .in_13(bus_cpu_system_gate_1_out_25), .in_14(bus_gate_6_out_23), .in_15(bus_cpu_system_gate_1_out_26),
    .in_16(bus_gate_6_out_24), .out_17(bus_gate_5_out_17), .out_18(bus_gate_5_out_18),
    .out_19(bus_gate_5_out_19), .out_20(bus_gate_5_out_20), .out_21(bus_gate_5_out_21),
    .out_22(bus_gate_5_out_22), .out_23(bus_gate_5_out_23), .out_24(bus_gate_5_out_24));
  Button button_1 (.out(button_1_out));
  Button button_2 (.out(button_2_out));
  input_buffer Inputer_buffer (
    .CLK(CLK_clk), .Reset(CLK_reset), .in_3(_0), .in_4(_1), .in_5(_2), .in_6(_3), .in_7(_4), .in_8(_5),
    .in_9(_6), .in_10(_7), .in_11(_8), .out_14(Inputer_buffer_out_14), .in_12(_9),
    .out_15(Inputer_buffer_out_15), .out_16(Inputer_buffer_out_16), .out_17(Inputer_buffer_out_17),
    .INP(IR_inp));
  digital_display display_buffer (
    .out_12(display_buffer_out_12), .out_13(display_buffer_out_13), .out_14(display_buffer_out_14),
    .out_15(display_buffer_out_15), .out_16(display_buffer_out_16), .out_17(display_buffer_out_17),
    .out_18(display_buffer_out_18), .out_19(display_buffer_out_19), .out_20(display_buffer_out_20),
    .out_21(display_buffer_out_21), .out_22(display_buffer_out_22), .out_23(display_buffer_out_23),
    .out_24(display_buffer_out_24), .out_25(display_buffer_out_25), .in_4(bus_gate_5_out_24),
    .in_5(bus_gate_5_out_23), .in_6(bus_gate_5_out_22), .in_7(bus_gate_5_out_21), .in_8(bus_gate_5_out_20),
    .in_9(bus_gate_5_out_19), .in_10(bus_gate_5_out_18), .in_11(bus_gate_5_out_17), .CLK(CLK_clk),
    .PRT(IR_prt), .Reset(CLK_reset));
  Button _128 (.out(_128_out));
  Button _64 (.out(_64_out));
  Button _32 (.out(_32_out));
  Button _16 (.out(_16_out));
  Button u__8 (.out(_8_out));
  Button u__4 (.out(_4_out));
  Button u__2 (.out(_2_out));
  Button u__1 (.out(_1_out));
  RAM RAM (
    .CLK(CLK_out_13), .input_mode(IR_ram_r_w), .in_22(mar_mbr_1_out_27), .in_23(mar_mbr_1_out_28),
    .Input_address(mar_mbr_1_out_29), .in_25(mar_mbr_1_out_30), .Input_data(bus_gate_5_out_24),
    .in_8(bus_gate_5_out_23), .in_10(bus_gate_5_out_22), .in_12(bus_gate_5_out_21),
    .in_14(bus_gate_5_out_20), .in_16(bus_gate_5_out_19), .in_18(bus_gate_5_out_18),
    .in_20(bus_gate_5_out_17), .out_29(RAM_out_29), .out_30(RAM_out_30), .out_31(RAM_out_31),
    .out_32(RAM_out_32), .out_33(RAM_out_33), .out_34(RAM_out_34), .out_35(RAM_out_35), .out_36(RAM_out_36),
    .in_1(CLK_clk), .RESET_data(or_1_out), .RESET_RAM(button_1_out), .CU(IR_to_ram), .out_28(RAM_out_28),
    .Program(button_2_out), .in_21(_1_out), .in_19(_2_out), .in_17(_4_out), .in_15(_8_out), .in_7(_128_out),
    .in_9(_64_out), .in_11(_32_out), .in_13(_16_out));
  _7_Segment_Display u_7_segment_display_1 (
    .g(display_buffer_out_12), .f(display_buffer_out_13), .a(display_buffer_out_14),
    .b(display_buffer_out_15), .e(display_buffer_out_16), .d(display_buffer_out_17), .c(display_buffer_out_18));  // open: dp
  _7_Segment_Display u_7_segment_display_2 (
    .g(display_buffer_out_19), .f(display_buffer_out_20), .a(display_buffer_out_21),
    .b(display_buffer_out_22), .e(display_buffer_out_23), .d(display_buffer_out_24), .c(display_buffer_out_25));  // open: dp
  BUS_gate bus_gate_6 (
    .in_1(Inputer_buffer_out_17), .in_2(RAM_out_36), .in_3(Inputer_buffer_out_16), .in_4(RAM_out_35),
    .in_5(Inputer_buffer_out_15), .in_6(RAM_out_34), .in_7(Inputer_buffer_out_14), .in_8(RAM_out_33),
    .in_9(RAM_out_32), .in_10(RAM_out_32), .in_11(RAM_out_31), .in_12(RAM_out_31), .in_13(RAM_out_30),
    .in_14(RAM_out_30), .in_15(RAM_out_29), .in_16(RAM_out_29), .out_17(bus_gate_6_out_17),
    .out_18(bus_gate_6_out_18), .out_19(bus_gate_6_out_19), .out_20(bus_gate_6_out_20),
    .out_21(bus_gate_6_out_21), .out_22(bus_gate_6_out_22), .out_23(bus_gate_6_out_23),
    .out_24(bus_gate_6_out_24));

  // Notes on the sheet:
  //   COMP 273- CPU project
  //   By Yi Tian Xu, Yang Ye
  //   --> click here to start computer
  //   After setting up RAM and the input key
  //   Enable ticks and the program will run itself
  //   CPU/System BUS gate
  //   CPU BUS 8 bits
  //   NOTE: RAM needs to be reseted each time the program runs
  //   Click on ON/OFF button to set PC to 0 and to clear all registers
  //   System BUS (13 bits)
  //   Select only one key before the start of the program
  //   Leave the input pin on during the entire program
  //   Display in Hex
endmodule

module half_adder (
  input  in_1,
  input  in_2,
  output out_3,
  output carry
);

  wire not_1_out, or_1_out;

  and and_1 (carry, in_1, in_2);
  or or_1 (or_1_out, in_1, in_2);
  not not_1 (not_1_out, carry);
  and and_2 (out_3, not_1_out, or_1_out);
endmodule

module full_adder (
  input  in_1,
  input  in_2,
  input  in_3,
  output out_4,
  output carry
);

  wire and_1_out, and_2_out, and_3_out, not_1_out, or_1_out;

  and and_1 (and_1_out, in_2, in_3);
  or or_1 (or_1_out, in_2, in_3);
  or or_2 (carry, and_1_out, and_2_out);
  not not_1 (not_1_out, and_1_out);
  and and_2 (and_2_out, in_1, or_1_out);
  and and_3 (and_3_out, not_1_out, or_1_out);
  xor xor_1 (out_4, in_1, and_3_out);
endmodule

module ALU__8_bit (
  input  Clock,
  input  in_2,
  input  ON_OFF,
  input  in_4,
  input  in_5,
  input  in_6,
  input  in_7,
  input  in_8,
  input  in_9,
  input  in_10,
  input  in_11,
  input  in_12,
  input  in_13,
  input  in_14,
  input  in_15,
  input  in_16,
  input  in_17,
  input  in_18,
  input  in_19,
  input  in_20,
  input  in_21,
  input  in_22,
  input  R_negative,
  input  L_negative,
  output to_CU,
  output out_26,
  output out_27,
  output out_28,
  output out_29,
  output out_30,
  output out_31,
  output out_32,
  output out_33,
  output out_34,
  output Zero,
  output Status,
  output Negative
);

  wire and_1_out, and_2_out, and_3_out, and_4_out, and_5_out, and_6_out, and_7_out, and_8_out, d_ff_1_q,
       d_ff_2_q, d_ff_3_q, d_ff_5_q, d_ff_7_q, d_ff_8_q, d_ff_9_q, d_ff_10_q, d_ff_11_q, d_ff_12_q,
       d_ff_13_q, d_ff_14_q, d_ff_15_q, d_ff_16_q, d_ff_17_q, d_ff_18_q, d_ff_19_q, d_ff_20_q, d_ff_21_q,
       d_ff_22_q, d_ff_23_q, d_ff_24_q, d_ff_25_q, d_ff_26_q, d_ff_27_q, d_ff_28_q, d_ff_29_q,
       Full_adder_2_carry, Full_adder_2_out_4, Full_adder_3_carry, Full_adder_3_out_4, Full_adder_4_carry,
       Full_adder_4_out_4, Full_adder_5_carry, Full_adder_5_out_4, Full_adder_6_carry, Full_adder_6_out_4,
       Full_adder_7_carry, Full_adder_7_out_4, Full_adder_8_out_4, Full_adder_carry, Full_adder_out_4,
       Half_adder_2_carry, Half_adder_2_out_3, Half_adder_3_carry, Half_adder_3_out_3, Half_adder_4_carry,
       Half_adder_4_out_3, Half_adder_5_carry, Half_adder_5_out_3, Half_adder_6_carry, Half_adder_6_out_3,
       Half_adder_7_carry, Half_adder_7_out_3, Half_adder_8_out_3, Half_adder_carry, Half_adder_out_3,
       L_out_21, L_out_22, L_out_23, L_out_24, L_out_25, L_out_26, L_out_27, L_out_28, multiplexer_1_out,
       multiplexer_2_out, multiplexer_3_out, multiplexer_4_out, multiplexer_5_out, multiplexer_6_out,
       multiplexer_7_out, multiplexer_8_out, multiplexer_9_out, multiplexer_10_out, multiplexer_11_out,
       multiplexer_12_out, multiplexer_13_out, multiplexer_14_out, multiplexer_15_out, multiplexer_16_out,
       not_1_out, not_2_out, not_3_out, not_4_out, not_5_out, not_6_out, not_7_out, not_8_out, not_9_out,
       not_10_out, not_11_out, not_12_out, not_13_out, not_14_out, not_15_out, not_16_out, not_17_out,
       not_18_out, not_19_out, not_20_out, not_21_out, not_22_out, not_23_out, not_24_out, not_25_out,
       not_26_out, or_1_out, or_2_out, or_3_out, R_out_21, R_out_22, R_out_23, R_out_24, R_out_25, R_out_26,
       R_out_27, R_out_28;

  or or_1 (or_1_out, in_13, in_22);
  D_Flip_Flop d_ff_1 (.Q(d_ff_1_q), .preset(or_1_out), .reset(or_2_out));  // open: clk, D, Qn, en
  or or_2 (or_2_out, in_4, out_26);
  not not_1 (not_1_out, Clock);
  D_Flip_Flop d_ff_2 (.clk(Clock), .D(d_ff_1_q), .Q(d_ff_2_q), .reset(in_4));  // open: Qn, preset, en
  register__8_bit R (
    .in_6(in_5), .in_7(in_6), .in_8(in_7), .in_9(in_8), .in_10(in_9), .in_11(in_10), .in_12(in_11),
    .in_13(in_12), .out_21(R_out_21), .out_22(R_out_22), .out_23(R_out_23), .out_24(R_out_24),
    .out_25(R_out_25), .out_26(R_out_26), .out_27(R_out_27), .out_28(R_out_28), .in_1(d_ff_2_q), .W_R(in_13),
    .Address(ON_OFF), .RESET(in_4));  // open: in_2, in_3, in_4, in_5, in_14, in_15, in_16, in_17
  register__8_bit L (
    .in_6(in_14), .in_7(in_15), .in_8(in_16), .in_9(in_17), .in_10(in_18), .in_11(in_19), .in_12(in_20),
    .in_13(in_21), .out_21(L_out_21), .out_22(L_out_22), .out_23(L_out_23), .out_24(L_out_24),
    .out_25(L_out_25), .out_26(L_out_26), .out_27(L_out_27), .out_28(L_out_28), .in_1(d_ff_2_q), .W_R(in_22),
    .Address(ON_OFF), .RESET(in_4));  // open: in_2, in_3, in_4, in_5, in_14, in_15, in_16, in_17
  D_Flip_Flop d_ff_3 (.Q(d_ff_3_q), .preset(in_2), .reset(or_3_out));  // open: clk, D, Qn, en
  or or_3 (or_3_out, in_4, to_CU);
  D_Flip_Flop d_ff_4 (.clk(not_1_out), .D(d_ff_2_q), .Q(out_26), .reset(in_4));  // open: Qn, preset, en
  D_Flip_Flop d_ff_5 (.clk(Clock), .D(d_ff_3_q), .Q(d_ff_5_q), .reset(in_4));  // open: Qn, preset, en
  not not_2 (not_2_out, Clock);
  D_Flip_Flop d_ff_6 (.clk(not_2_out), .D(d_ff_5_q), .Q(to_CU), .reset(in_4));  // open: Qn, preset, en
  D_Flip_Flop d_ff_7 (.clk(d_ff_3_q), .D(R_out_28), .Q(d_ff_7_q), .reset(in_4));  // open: Qn, preset, en
  D_Flip_Flop d_ff_8 (.clk(d_ff_3_q), .D(L_out_28), .Q(d_ff_8_q), .reset(in_4));  // open: Qn, preset, en
  D_Flip_Flop d_ff_9 (.clk(d_ff_3_q), .D(R_out_27), .Q(d_ff_9_q), .reset(in_4));  // open: Qn, preset, en
  D_Flip_Flop d_ff_10 (.clk(d_ff_3_q), .D(L_out_27), .Q(d_ff_10_q), .reset(in_4));  // open: Qn, preset, en
  D_Flip_Flop d_ff_11 (.clk(d_ff_3_q), .D(R_out_26), .Q(d_ff_11_q), .reset(in_4));  // open: Qn, preset, en
  D_Flip_Flop d_ff_12 (.clk(d_ff_3_q), .D(L_out_26), .Q(d_ff_12_q), .reset(in_4));  // open: Qn, preset, en
  D_Flip_Flop d_ff_13 (.clk(d_ff_3_q), .D(R_out_25), .Q(d_ff_13_q), .reset(in_4));  // open: Qn, preset, en
  D_Flip_Flop d_ff_14 (.clk(d_ff_3_q), .D(L_out_25), .Q(d_ff_14_q), .reset(in_4));  // open: Qn, preset, en
  D_Flip_Flop d_ff_15 (.clk(d_ff_3_q), .D(R_out_24), .Q(d_ff_15_q), .reset(in_4));  // open: Qn, preset, en
  D_Flip_Flop d_ff_16 (.clk(d_ff_3_q), .D(L_out_24), .Q(d_ff_16_q), .reset(in_4));  // open: Qn, preset, en
  D_Flip_Flop d_ff_17 (.clk(d_ff_3_q), .D(R_out_23), .Q(d_ff_17_q), .reset(in_4));  // open: Qn, preset, en
  D_Flip_Flop d_ff_18 (.clk(d_ff_3_q), .D(L_out_23), .Q(d_ff_18_q), .reset(in_4));  // open: Qn, preset, en
  D_Flip_Flop d_ff_19 (.clk(d_ff_3_q), .D(R_out_22), .Q(d_ff_19_q), .reset(in_4));  // open: Qn, preset, en
  D_Flip_Flop d_ff_20 (.clk(d_ff_3_q), .D(L_out_22), .Q(d_ff_20_q), .reset(in_4));  // open: Qn, preset, en
  D_Flip_Flop d_ff_21 (.clk(d_ff_3_q), .D(R_out_21), .Q(d_ff_21_q), .reset(in_4));  // open: Qn, preset, en
  D_Flip_Flop d_ff_22 (.clk(d_ff_3_q), .D(L_out_21), .Q(d_ff_22_q), .reset(in_4));  // open: Qn, preset, en
  not not_3 (not_3_out, d_ff_7_q);
  not not_4 (not_4_out, d_ff_8_q);
  not not_5 (not_5_out, d_ff_9_q);
  not not_6 (not_6_out, d_ff_10_q);
  not not_7 (not_7_out, d_ff_11_q);
  not not_8 (not_8_out, d_ff_12_q);
  not not_9 (not_9_out, d_ff_13_q);
  not not_10 (not_10_out, d_ff_14_q);
  not not_11 (not_11_out, d_ff_15_q);
  not not_12 (not_12_out, d_ff_16_q);
  not not_13 (not_13_out, d_ff_17_q);
  not not_14 (not_14_out, d_ff_18_q);
  not not_15 (not_15_out, d_ff_19_q);
  not not_16 (not_16_out, d_ff_20_q);
  not not_17 (not_17_out, d_ff_21_q);
  not not_18 (not_18_out, d_ff_22_q);
  Multiplexer multiplexer_1 (.in0(d_ff_7_q), .in1(not_3_out), .out(multiplexer_1_out), .sel(R_negative), .en(ON_OFF));
  Multiplexer multiplexer_2 (.in0(d_ff_8_q), .in1(not_4_out), .out(multiplexer_2_out), .sel(L_negative), .en(ON_OFF));
  Multiplexer multiplexer_3 (.in0(d_ff_9_q), .in1(not_5_out), .out(multiplexer_3_out), .sel(R_negative), .en(ON_OFF));
  Multiplexer multiplexer_4 (.in0(d_ff_10_q), .in1(not_6_out), .out(multiplexer_4_out), .sel(L_negative), .en(ON_OFF));
  Multiplexer multiplexer_5 (.in0(d_ff_11_q), .in1(not_7_out), .out(multiplexer_5_out), .sel(R_negative), .en(ON_OFF));
  Multiplexer multiplexer_6 (.in0(d_ff_12_q), .in1(not_8_out), .out(multiplexer_6_out), .sel(L_negative), .en(ON_OFF));
  Multiplexer multiplexer_7 (.in0(d_ff_13_q), .in1(not_9_out), .out(multiplexer_7_out), .sel(R_negative), .en(ON_OFF));
  Multiplexer multiplexer_8 (.in0(d_ff_14_q), .in1(not_10_out), .out(multiplexer_8_out), .sel(L_negative), .en(ON_OFF));
  Multiplexer multiplexer_9 (.in0(d_ff_15_q), .in1(not_11_out), .out(multiplexer_9_out), .sel(R_negative), .en(ON_OFF));
  Multiplexer multiplexer_10 (
    .in0(d_ff_16_q), .in1(not_12_out), .out(multiplexer_10_out), .sel(L_negative), .en(ON_OFF));
  Multiplexer multiplexer_11 (
    .in0(d_ff_17_q), .in1(not_13_out), .out(multiplexer_11_out), .sel(R_negative), .en(ON_OFF));
  Multiplexer multiplexer_12 (
    .in0(d_ff_18_q), .in1(not_14_out), .out(multiplexer_12_out), .sel(L_negative), .en(ON_OFF));
  Multiplexer multiplexer_13 (
    .in0(d_ff_19_q), .in1(not_15_out), .out(multiplexer_13_out), .sel(R_negative), .en(ON_OFF));
  Multiplexer multiplexer_14 (
    .in0(d_ff_20_q), .in1(not_16_out), .out(multiplexer_14_out), .sel(L_negative), .en(ON_OFF));
  Multiplexer multiplexer_15 (
    .in0(d_ff_21_q), .in1(not_17_out), .out(multiplexer_15_out), .sel(R_negative), .en(ON_OFF));
  Multiplexer multiplexer_16 (
    .in0(d_ff_22_q), .in1(not_18_out), .out(multiplexer_16_out), .sel(L_negative), .en(ON_OFF));
  and and_1 (and_1_out, R_negative, 1'b1);
  and and_2 (and_2_out, 1'b1, L_negative);
  full_adder Full_adder (
    .in_2(multiplexer_1_out), .in_3(multiplexer_2_out), .out_4(Full_adder_out_4), .in_1(and_2_out),
    .carry(Full_adder_carry));
  full_adder Full_adder_2 (
    .in_2(multiplexer_3_out), .in_3(multiplexer_4_out), .out_4(Full_adder_2_out_4), .in_1(Full_adder_carry),
    .carry(Full_adder_2_carry));
  full_adder Full_adder_3 (
    .in_2(multiplexer_5_out), .in_3(multiplexer_6_out), .out_4(Full_adder_3_out_4),
    .in_1(Full_adder_2_carry), .carry(Full_adder_3_carry));
  full_adder Full_adder_4 (
    .in_2(multiplexer_7_out), .in_3(multiplexer_8_out), .out_4(Full_adder_4_out_4),
    .in_1(Full_adder_3_carry), .carry(Full_adder_4_carry));
  full_adder Full_adder_5 (
    .in_2(multiplexer_9_out), .in_3(multiplexer_10_out), .out_4(Full_adder_5_out_4),
    .in_1(Full_adder_4_carry), .carry(Full_adder_5_carry));
  full_adder Full_adder_6 (
    .in_2(multiplexer_11_out), .in_3(multiplexer_12_out), .out_4(Full_adder_6_out_4),
    .in_1(Full_adder_5_carry), .carry(Full_adder_6_carry));
  full_adder Full_adder_7 (
    .in_2(multiplexer_13_out), .in_3(multiplexer_14_out), .out_4(Full_adder_7_out_4),
    .in_1(Full_adder_6_carry), .carry(Full_adder_7_carry));
  full_adder Full_adder_8 (
    .in_2(multiplexer_15_out), .in_3(multiplexer_16_out), .out_4(Full_adder_8_out_4),
    .in_1(Full_adder_7_carry), .carry(Status));
  half_adder Half_adder (.in_1(and_1_out), .in_2(Full_adder_out_4), .out_3(Half_adder_out_3), .carry(Half_adder_carry));
  half_adder Half_adder_2 (
    .in_1(Half_adder_carry), .in_2(Full_adder_2_out_4), .out_3(Half_adder_2_out_3), .carry(Half_adder_2_carry));
  half_adder Half_adder_3 (
    .in_1(Half_adder_2_carry), .in_2(Full_adder_3_out_4), .out_3(Half_adder_3_out_3),
    .carry(Half_adder_3_carry));
  half_adder Half_adder_4 (
    .in_1(Half_adder_3_carry), .in_2(Full_adder_4_out_4), .out_3(Half_adder_4_out_3),
    .carry(Half_adder_4_carry));
  half_adder Half_adder_5 (
    .in_1(Half_adder_4_carry), .in_2(Full_adder_5_out_4), .out_3(Half_adder_5_out_3),
    .carry(Half_adder_5_carry));
  half_adder Half_adder_6 (
    .in_1(Half_adder_5_carry), .in_2(Full_adder_6_out_4), .out_3(Half_adder_6_out_3),
    .carry(Half_adder_6_carry));
  half_adder Half_adder_7 (
    .in_1(Half_adder_6_carry), .in_2(Full_adder_7_out_4), .out_3(Half_adder_7_out_3),
    .carry(Half_adder_7_carry));
  half_adder Half_adder_8 (
    .in_1(Half_adder_7_carry), .in_2(Full_adder_8_out_4), .out_3(Half_adder_8_out_3));  // open: carry
  D_Flip_Flop d_ff_23 (.clk(d_ff_5_q), .D(Half_adder_out_3), .Q(d_ff_23_q), .reset(in_4));  // open: Qn, preset, en
  D_Flip_Flop d_ff_24 (.clk(d_ff_5_q), .D(Half_adder_2_out_3), .Q(d_ff_24_q), .reset(in_4));  // open: Qn, preset, en
  not not_19 (not_19_out, d_ff_24_q);
  not not_20 (not_20_out, d_ff_23_q);
  and and_3 (and_3_out, not_20_out, not_19_out);
  D_Flip_Flop d_ff_25 (.clk(d_ff_5_q), .D(Half_adder_3_out_3), .Q(d_ff_25_q), .reset(in_4));  // open: Qn, preset, en
  and and_4 (and_4_out, and_3_out, not_21_out);
  D_Flip_Flop d_ff_26 (.clk(d_ff_5_q), .D(Half_adder_4_out_3), .Q(d_ff_26_q), .reset(in_4));  // open: Qn, preset, en
  D_Flip_Flop d_ff_27 (.clk(d_ff_5_q), .D(Half_adder_5_out_3), .Q(d_ff_27_q), .reset(in_4));  // open: Qn, preset, en
  D_Flip_Flop d_ff_28 (.clk(d_ff_5_q), .D(Half_adder_6_out_3), .Q(d_ff_28_q), .reset(in_4));  // open: Qn, preset, en
  D_Flip_Flop d_ff_29 (.clk(d_ff_5_q), .D(Half_adder_7_out_3), .Q(d_ff_29_q), .reset(in_4));  // open: Qn, preset, en
  D_Flip_Flop d_ff_30 (.clk(d_ff_5_q), .D(Half_adder_8_out_3), .Q(Negative), .reset(in_4));  // open: Qn, preset, en
  not not_21 (not_21_out, d_ff_25_q);
  not not_22 (not_22_out, d_ff_26_q);
  and and_5 (and_5_out, and_4_out, not_22_out);
  not not_23 (not_23_out, d_ff_27_q);
  and and_6 (and_6_out, and_5_out, not_23_out);
  not not_24 (not_24_out, d_ff_28_q);
  and and_7 (and_7_out, and_6_out, not_24_out);
  not not_25 (not_25_out, d_ff_29_q);
  and and_8 (and_8_out, and_7_out, not_25_out);
  not not_26 (not_26_out, Negative);
  and and_9 (Zero, and_8_out, to_CU, not_26_out);
  register__8_bit R_2 (
    .in_6(Negative), .in_7(d_ff_29_q), .in_8(d_ff_28_q), .in_9(d_ff_27_q), .in_10(d_ff_26_q),
    .in_11(d_ff_25_q), .in_12(d_ff_24_q), .in_13(d_ff_23_q), .out_21(out_27), .out_22(out_28),
    .out_23(out_29), .out_24(out_30), .out_25(out_31), .out_26(out_32), .out_27(out_33), .out_28(out_34),
    .in_1(to_CU), .W_R(d_ff_5_q), .Address(ON_OFF), .RESET(in_4));  // open: in_2, in_3, in_4, in_5, in_14, in_15, in_16, in_17

  // Notes on the sheet:
  //   For 2's compliment
endmodule

module ALU__4_bit (
  input  CLK,
  input  CONSTANT,
  input  in_3,
  input  in_4,
  input  in_5,
  input  in_6,
  input  BZ,
  input  in_8,
  output out_9,
  output out_10,
  output out_11,
  output out_12
);

  wire d_ff_1_q, d_ff_2_q, d_ff_3_q, d_ff_4_q, half_adder_1_carry, half_adder_1_out_3, half_adder_2_carry,
       half_adder_2_out_3, half_adder_3_carry, half_adder_3_out_3, half_adder_4_out_3, not_1_out;

  half_adder half_adder_1 (.in_1(CONSTANT), .in_2(in_6), .out_3(half_adder_1_out_3), .carry(half_adder_1_carry));
  half_adder half_adder_2 (
    .in_1(half_adder_1_carry), .in_2(in_5), .out_3(half_adder_2_out_3), .carry(half_adder_2_carry));
  half_adder half_adder_3 (
    .in_1(half_adder_2_carry), .in_2(in_4), .out_3(half_adder_3_out_3), .carry(half_adder_3_carry));
  half_adder half_adder_4 (.in_1(half_adder_3_carry), .in_2(in_3), .out_3(half_adder_4_out_3));  // open: carry
  D_Flip_Flop d_ff_1 (.clk(CLK), .D(half_adder_1_out_3), .Q(d_ff_1_q), .reset(BZ));  // open: Qn, preset, en
  D_Flip_Flop d_ff_2 (.clk(CLK), .D(half_adder_2_out_3), .Q(d_ff_2_q), .reset(BZ));  // open: Qn, preset, en
  D_Flip_Flop d_ff_3 (.clk(CLK), .D(half_adder_3_out_3), .Q(d_ff_3_q), .reset(BZ));  // open: Qn, preset, en
  D_Flip_Flop d_ff_4 (.clk(CLK), .D(half_adder_4_out_3), .Q(d_ff_4_q), .reset(BZ));  // open: Qn, preset, en
  and and_1 (out_12, d_ff_1_q, not_1_out);
  and and_2 (out_11, d_ff_2_q, not_1_out);
  and and_3 (out_10, d_ff_3_q, not_1_out);
  and and_4 (out_9, d_ff_4_q, not_1_out);
  not not_1 (not_1_out, in_8);

  // Notes on the sheet:
  //   Reset
endmodule

module RAM (
  input  in_1,
  input  CLK,
  input  CU,
  input  RESET_data,
  input  RESET_RAM,
  input  Input_data,
  input  in_7,
  input  in_8,
  input  in_9,
  input  in_10,
  input  in_11,
  input  in_12,
  input  in_13,
  input  in_14,
  input  in_15,
  input  in_16,
  input  in_17,
  input  in_18,
  input  in_19,
  input  in_20,
  input  in_21,
  input  in_22,
  input  in_23,
  input  Input_address,
  input  in_25,
  input  input_mode,
  input  Program,
  output out_28,
  output out_29,
  output out_30,
  output out_31,
  output out_32,
  output out_33,
  output out_34,
  output out_35,
  output out_36
);

  wire _0000_out_21, _0000_out_22, _0000_out_23, _0000_out_24, _0000_out_25, _0000_out_26, _0000_out_27,
       _0000_out_28, _0001_out_21, _0001_out_22, _0001_out_23, _0001_out_24, _0001_out_25, _0001_out_26,
       _0001_out_27, _0001_out_28, _0010_out_21, _0010_out_22, _0010_out_23, _0010_out_24, _0010_out_25,
       _0010_out_26, _0010_out_27, _0010_out_28, _0011_out_21, _0011_out_22, _0011_out_23, _0011_out_24,
       _0011_out_25, _0011_out_26, _0011_out_27, _0011_out_28, _0100_out_21, _0100_out_22, _0100_out_23,
       _0100_out_24, _0100_out_25, _0100_out_26, _0100_out_27, _0100_out_28, _0101_out_21, _0101_out_22,
       _0101_out_23, _0101_out_24, _0101_out_25, _0101_out_26, _0101_out_27, _0101_out_28, _0110_out_21,
       _0110_out_22, _0110_out_23, _0110_out_24, _0110_out_25, _0110_out_26, _0110_out_27, _0110_out_28,
       _0111_out_21, _0111_out_22, _0111_out_23, _0111_out_24, _0111_out_25, _0111_out_26, _0111_out_27,
       _0111_out_28, _1000_out_21, _1000_out_22, _1000_out_23, _1000_out_24, _1000_out_25, _1000_out_26,
       _1000_out_27, _1000_out_28, _1001_out_21, _1001_out_22, _1001_out_23, _1001_out_24, _1001_out_25,
       _1001_out_26, _1001_out_27, _1001_out_28, _1010_out_21, _1010_out_22, _1010_out_23, _1010_out_24,
       _1010_out_25, _1010_out_26, _1010_out_27, _1010_out_28, _1011_out_21, _1011_out_22, _1011_out_23,
       _1011_out_24, _1011_out_25, _1011_out_26, _1011_out_27, _1011_out_28, _1100_out_21, _1100_out_22,
       _1100_out_23, _1100_out_24, _1100_out_25, _1100_out_26, _1100_out_27, _1100_out_28, _1101_out_21,
       _1101_out_22, _1101_out_23, _1101_out_24, _1101_out_25, _1101_out_26, _1101_out_27, _1101_out_28,
       _1110_out_21, _1110_out_22, _1110_out_23, _1110_out_24, _1110_out_25, _1110_out_26, _1110_out_27,
       _1110_out_28, _1111_out_21, _1111_out_22, _1111_out_23, _1111_out_24, _1111_out_25, _1111_out_26,
       _1111_out_27, _1111_out_28, Address_register_out_9, Address_register_out_10, Address_register_out_11,
       Address_register_out_12, and_1_out, and_2_out, and_3_out, and_4_out, and_5_out, and_6_out, and_7_out,
       and_8_out, and_9_out, and_10_out, and_11_out, and_12_out, and_13_out, and_14_out, and_15_out,
       and_25_out, and_26_out, and_27_out, and_28_out, and_29_out, and_30_out, and_31_out, and_32_out,
       and_33_out, and_34_out, and_35_out, and_36_out, and_37_out, and_38_out, and_39_out, and_40_out,
       and_41_out, and_42_out, and_43_out, and_44_out, and_45_out, and_46_out, and_47_out, and_48_out,
       CU_status_q, d_ff_1_q, d_ff_2_q, d_ff_3_q, d_ff_4_q, d_ff_5_q, d_ff_6_q, Data_register_out_21,
       Data_register_out_22, Data_register_out_23, Data_register_out_24, Data_register_out_25,
       Data_register_out_26, Data_register_out_27, Data_register_out_28, not_1_out, not_2_out, not_3_out,
       not_4_out, not_5_out, not_6_out, not_7_out, not_8_out, not_9_out, not_10_out, not_11_out, not_12_out,
       not_13_out, not_14_out, not_15_out, not_16_out, not_17_out, not_18_out, not_19_out, not_20_out,
       not_21_out, not_22_out, not_23_out, not_24_out, not_25_out, not_26_out, not_27_out, not_28_out,
       not_29_out, not_30_out, not_31_out, not_32_out, not_33_out, not_34_out, not_35_out, not_36_out,
       not_37_out, not_38_out, not_39_out, not_40_out, not_41_out, not_42_out, or_1_out, or_2_out, or_3_out,
       or_4_out, or_5_out, or_6_out, or_7_out, or_8_out, or_9_out, or_10_out, or_11_out, or_12_out,
       or_13_out, or_14_out, or_15_out, or_16_out, or_17_out, or_18_out, or_19_out, or_20_out, or_21_out,
       or_22_out, or_23_out, or_24_out, or_25_out, or_26_out, or_27_out, or_28_out, or_29_out, or_30_out,
       or_31_out, or_32_out, or_33_out, or_34_out, or_35_out, or_36_out, or_37_out, or_38_out, or_39_out,
       or_40_out, or_41_out, or_42_out, or_43_out, or_44_out, or_45_out, or_46_out, or_47_out, or_48_out,
       or_49_out, or_50_out, or_51_out, or_52_out, or_53_out, or_54_out, or_55_out, or_56_out, or_57_out,
       or_58_out, or_59_out, or_60_out, or_61_out, or_62_out, or_63_out, or_64_out, or_65_out, or_66_out,
       or_67_out, or_68_out, or_69_out, or_70_out, or_71_out, or_72_out, or_73_out, or_74_out, or_75_out,
       or_76_out, or_77_out, or_78_out, or_79_out, or_80_out, or_81_out, or_82_out, or_83_out, or_84_out,
       or_85_out, or_86_out, or_87_out, or_88_out, or_89_out, or_90_out, or_91_out, or_92_out, or_93_out,
       or_94_out, or_95_out, or_96_out, or_97_out, or_98_out, or_99_out, or_100_out, or_101_out, or_102_out,
       or_103_out, or_104_out, or_105_out, or_106_out, or_107_out, or_108_out, or_109_out, or_110_out,
       or_111_out, or_112_out, or_113_out, or_114_out, or_115_out, or_116_out, or_117_out, or_118_out,
       or_119_out, or_120_out, or_121_out, or_122_out, or_123_out, or_124_out, or_125_out, or_126_out,
       or_127_out, or_128_out, or_129_out, or_130_out, or_131_out, or_132_out, or_133_out, or_134_out,
       read_write_q, Register_status_q;

  D_Flip_Flop CU_status (.Q(CU_status_q), .preset(CU), .reset(RESET_data));  // open: clk, D, Qn, en
  or or_1 (or_1_out, CLK, CU);
  or or_2 (or_2_out, and_2_out, and_3_out);
  and and_1 (and_1_out, not_6_out, Input_data);
  D_Flip_Flop d_ff_1 (.Q(d_ff_1_q), .preset(or_1_out), .reset(or_3_out));  // open: clk, D, Qn, en
  or or_3 (or_3_out, RESET_data, d_ff_2_q);
  and and_2 (and_2_out, not_6_out, or_4_out);
  and and_3 (and_3_out, d_ff_4_q, not_1_out);
  not not_1 (not_1_out, not_6_out);
  and and_4 (and_4_out, not_6_out, in_8);
  and and_5 (and_5_out, not_6_out, in_10);
  D_Flip_Flop d_ff_2 (.clk(in_1), .D(d_ff_1_q), .Q(d_ff_2_q), .reset(RESET_data));  // open: Qn, preset, en
  or or_4 (or_4_out, d_ff_1_q, d_ff_2_q);
  and and_6 (and_6_out, not_6_out, in_12);
  and and_7 (and_7_out, not_6_out, in_14);
  not not_2 (not_2_out, in_1);
  and and_8 (and_8_out, not_2_out, not_3_out);
  not not_3 (not_3_out, not_6_out);
  and and_9 (and_9_out, not_6_out, in_16);
  and and_10 (and_10_out, not_6_out, in_18);
  not not_4 (not_4_out, not_2_out);
  D_Flip_Flop d_ff_3 (.clk(not_2_out), .D(d_ff_2_q), .Q(d_ff_3_q), .reset(RESET_data));  // open: Qn, preset, en
  and and_11 (and_11_out, and_8_out, d_ff_3_q);
  and and_12 (and_12_out, d_ff_2_q, not_5_out);
  not not_5 (not_5_out, and_8_out);
  and and_13 (and_13_out, not_6_out, in_20);
  or or_5 (or_5_out, and_13_out, or_22_out);
  not not_6 (not_6_out, not_10_out);
  not not_7 (not_7_out, not_4_out);
  D_Flip_Flop d_ff_4 (.clk(not_4_out), .D(d_ff_3_q), .Q(d_ff_4_q), .reset(RESET_data));  // open: Qn, preset, en
  or or_6 (or_6_out, and_9_out, or_20_out);
  or or_7 (or_7_out, and_10_out, or_21_out);
  not not_8 (not_8_out, not_7_out);
  D_Flip_Flop d_ff_5 (.clk(not_7_out), .D(d_ff_4_q), .Q(d_ff_5_q), .reset(RESET_data));  // open: Qn, preset, en
  or or_8 (or_8_out, and_6_out, or_18_out);
  or or_9 (or_9_out, and_7_out, or_19_out);
  D_Flip_Flop d_ff_6 (.clk(not_8_out), .D(d_ff_5_q), .Q(d_ff_6_q), .reset(RESET_data));  // open: Qn, preset, en
  or or_10 (or_10_out, and_4_out, or_16_out);
  or or_11 (or_11_out, and_5_out, or_17_out);
  D_Flip_Flop Register_status (.Q(Register_status_q), .preset(or_1_out), .reset(RESET_data));  // open: clk, D, Qn, en
  not not_9 (not_9_out, d_ff_5_q);
  and and_14 (and_14_out, not_9_out, d_ff_6_q);
  or or_12 (or_12_out, and_1_out, or_15_out);
  and and_15 (and_15_out, not_6_out, d_ff_4_q);
  or or_13 (or_13_out, and_15_out, d_ff_5_q);
  register__8_bit Data_register (
    .in_6(or_12_out), .in_7(or_10_out), .in_8(or_11_out), .in_9(or_8_out), .in_10(or_9_out),
    .in_11(or_6_out), .in_12(or_7_out), .in_13(or_5_out), .out_21(Data_register_out_21),
    .out_22(Data_register_out_22), .out_23(Data_register_out_23), .out_24(Data_register_out_24),
    .out_25(Data_register_out_25), .out_26(Data_register_out_26), .out_27(Data_register_out_27),
    .out_28(Data_register_out_28), .in_1(or_13_out), .W_R(or_2_out), .Address(Register_status_q),
    .RESET(RESET_data));  // open: in_2, in_3, in_4, in_5, in_14, in_15, in_16, in_17
  and and_16 (out_36, Data_register_out_28, not_10_out);
  and and_17 (out_35, Data_register_out_27, not_10_out);
  and and_18 (out_33, Data_register_out_25, not_10_out);
  and and_19 (out_34, Data_register_out_26, not_10_out);
  or or_14 (or_14_out, and_12_out, and_11_out);
  and and_20 (out_32, Data_register_out_24, not_10_out);
  and and_21 (out_31, Data_register_out_23, not_10_out);
  and and_22 (out_30, Data_register_out_22, not_10_out);
  and and_23 (out_28, CU_status_q, and_14_out);
  not not_10 (not_10_out, read_write_q);
  and and_24 (out_29, Data_register_out_21, not_10_out);
  and and_25 (and_25_out, Data_register_out_21, read_write_q);
  and and_26 (and_26_out, Data_register_out_22, read_write_q);
  and and_27 (and_27_out, Data_register_out_23, read_write_q);
  and and_28 (and_28_out, Data_register_out_24, read_write_q);
  and and_29 (and_29_out, Data_register_out_25, read_write_q);
  and and_30 (and_30_out, Data_register_out_26, read_write_q);
  and and_31 (and_31_out, Data_register_out_27, read_write_q);
  and and_32 (and_32_out, Data_register_out_28, read_write_q);
  register__4_bits Address_register (
    .in_2(in_22), .in_3(in_23), .in_4(Input_address), .in_5(in_25), .out_9(Address_register_out_9),
    .out_10(Address_register_out_10), .out_11(Address_register_out_11), .out_12(Address_register_out_12),
    .in_1(or_14_out), .Address(Register_status_q), .W_R(or_4_out), .in_6(RESET_data));
  or or_15 (or_15_out, _0000_out_21, or_23_out);
  or or_16 (or_16_out, _0000_out_22, or_24_out);
  or or_17 (or_17_out, _0000_out_23, or_25_out);
  or or_18 (or_18_out, _0000_out_24, or_26_out);
  or or_19 (or_19_out, _0000_out_25, or_27_out);
  or or_20 (or_20_out, _0000_out_26, or_28_out);
  or or_21 (or_21_out, _0000_out_27, or_29_out);
  or or_22 (or_22_out, _0000_out_28, or_30_out);
  and and_33 (and_33_out, not_12_out, not_13_out, not_11_out, not_14_out);
  not not_11 (not_11_out, Address_register_out_11);
  not not_12 (not_12_out, Address_register_out_9);
  not not_13 (not_13_out, Address_register_out_10);
  register__8_bit _0000 (
    .in_6(and_25_out), .in_7(and_26_out), .in_8(and_27_out), .in_9(and_28_out), .in_10(and_29_out),
    .in_11(and_30_out), .in_12(and_31_out), .in_13(and_32_out), .out_21(_0000_out_21), .out_22(_0000_out_22),
    .out_23(_0000_out_23), .out_24(_0000_out_24), .out_25(_0000_out_25), .out_26(_0000_out_26),
    .out_27(_0000_out_27), .out_28(_0000_out_28), .in_1(d_ff_5_q), .W_R(read_write_q), .Address(and_33_out),
    .RESET(RESET_RAM), .in_5(Program));  // open: in_2, in_3, in_4, in_14, in_15, in_16, in_17
  not not_14 (not_14_out, Address_register_out_12);
  D_Flip_Flop read_write (.Q(read_write_q), .preset(input_mode), .reset(RESET_data));  // open: clk, D, Qn, en
  or or_23 (or_23_out, or_31_out, _0001_out_21);
  or or_24 (or_24_out, or_32_out, _0001_out_22);
  or or_25 (or_25_out, or_33_out, _0001_out_23);
  or or_26 (or_26_out, or_34_out, _0001_out_24);
  or or_27 (or_27_out, or_35_out, _0001_out_25);
  or or_28 (or_28_out, or_36_out, _0001_out_26);
  or or_29 (or_29_out, or_37_out, _0001_out_27);
  or or_30 (or_30_out, or_38_out, _0001_out_28);
  and and_34 (and_34_out, not_17_out, not_16_out, not_15_out, Address_register_out_12);
  not not_15 (not_15_out, Address_register_out_11);
  not not_16 (not_16_out, Address_register_out_10);
  not not_17 (not_17_out, Address_register_out_9);
  register__8_bit _0001 (
    .in_6(and_25_out), .in_7(and_26_out), .in_8(and_27_out), .in_9(and_28_out), .in_10(and_29_out),
    .in_11(and_30_out), .in_12(and_31_out), .in_13(and_32_out), .out_21(_0001_out_21), .out_22(_0001_out_22),
    .out_23(_0001_out_23), .out_24(_0001_out_24), .out_25(_0001_out_25), .out_26(_0001_out_26),
    .out_27(_0001_out_27), .out_28(_0001_out_28), .in_1(d_ff_5_q), .W_R(read_write_q), .Address(and_34_out),
    .RESET(RESET_RAM), .in_2(Program), .in_4(Program), .in_5(Program), .in_16(Program));  // open: in_3, in_14, in_15, in_17
  or or_31 (or_31_out, _0010_out_21, or_39_out);
  or or_32 (or_32_out, _0010_out_22, or_40_out);
  or or_33 (or_33_out, _0010_out_23, or_41_out);
  or or_34 (or_34_out, _0010_out_24, or_42_out);
  or or_35 (or_35_out, _0010_out_25, or_43_out);
  or or_36 (or_36_out, _0010_out_26, or_44_out);
  or or_37 (or_37_out, _0010_out_27, or_45_out);
  or or_38 (or_38_out, _0010_out_28, or_46_out);
  and and_35 (and_35_out, not_19_out, not_20_out, not_18_out, Address_register_out_11);
  not not_18 (not_18_out, Address_register_out_12);
  not not_19 (not_19_out, Address_register_out_9);
  not not_20 (not_20_out, Address_register_out_10);
  register__8_bit _0010 (
    .in_6(and_25_out), .in_7(and_26_out), .in_8(and_27_out), .in_9(and_28_out), .in_10(and_29_out),
    .in_11(and_30_out), .in_12(and_31_out), .in_13(and_32_out), .out_21(_0010_out_21), .out_22(_0010_out_22),
    .out_23(_0010_out_23), .out_24(_0010_out_24), .out_25(_0010_out_25), .out_26(_0010_out_26),
    .out_27(_0010_out_27), .out_28(_0010_out_28), .in_1(d_ff_5_q), .W_R(read_write_q), .Address(and_35_out),
    .RESET(RESET_RAM), .in_3(Program), .in_5(Program), .in_14(Program), .in_15(Program), .in_17(Program));  // open: in_2, in_4, in_16
  or or_39 (or_39_out, or_47_out, _0011_out_21);
  or or_40 (or_40_out, or_48_out, _0011_out_22);
  or or_41 (or_41_out, or_49_out, _0011_out_23);
  or or_42 (or_42_out, or_50_out, _0011_out_24);
  or or_43 (or_43_out, or_51_out, _0011_out_25);
  or or_44 (or_44_out, or_52_out, _0011_out_26);
  or or_45 (or_45_out, or_53_out, _0011_out_27);
  or or_46 (or_46_out, or_54_out, _0011_out_28);
  and and_36 (and_36_out, not_21_out, not_22_out, Address_register_out_11, Address_register_out_12);
  not not_21 (not_21_out, Address_register_out_9);
  not not_22 (not_22_out, Address_register_out_10);
  register__8_bit _0011 (
    .in_6(and_25_out), .in_7(and_26_out), .in_8(and_27_out), .in_9(and_28_out), .in_10(and_29_out),
    .in_11(and_30_out), .in_12(and_31_out), .in_13(and_32_out), .out_21(_0011_out_21), .out_22(_0011_out_22),
    .out_23(_0011_out_23), .out_24(_0011_out_24), .out_25(_0011_out_25), .out_26(_0011_out_26),
    .out_27(_0011_out_27), .out_28(_0011_out_28), .in_1(d_ff_5_q), .W_R(read_write_q), .Address(and_36_out),
    .RESET(RESET_RAM), .in_3(Program), .in_5(Program), .in_14(Program), .in_15(Program), .in_16(Program));  // open: in_2, in_4, in_17
  or or_47 (or_47_out, _0100_out_21, or_55_out);
  or or_48 (or_48_out, _0100_out_22, or_56_out);
  or or_49 (or_49_out, _0100_out_23, or_57_out);
  or or_50 (or_50_out, _0100_out_24, or_58_out);
  or or_51 (or_51_out, _0100_out_25, or_59_out);
  or or_52 (or_52_out, _0100_out_26, or_60_out);
  or or_53 (or_53_out, _0100_out_27, or_61_out);
  or or_54 (or_54_out, _0100_out_28, or_62_out);
  register__8_bit _0100 (
    .in_6(and_25_out), .in_7(and_26_out), .in_8(and_27_out), .in_9(and_28_out), .in_10(and_29_out),
    .in_11(and_30_out), .in_12(and_31_out), .in_13(and_32_out), .out_21(_0100_out_21), .out_22(_0100_out_22),
    .out_23(_0100_out_23), .out_24(_0100_out_24), .out_25(_0100_out_25), .out_26(_0100_out_26),
    .out_27(_0100_out_27), .out_28(_0100_out_28), .in_1(d_ff_5_q), .W_R(read_write_q), .Address(and_37_out),
    .RESET(RESET_RAM), .in_4(Program), .in_16(Program));  // open: in_2, in_3, in_5, in_14, in_15, in_17
  and and_37 (and_37_out, not_23_out, not_25_out, not_24_out, Address_register_out_10);
  not not_23 (not_23_out, Address_register_out_9);
  not not_24 (not_24_out, Address_register_out_12);
  not not_25 (not_25_out, Address_register_out_11);
  or or_55 (or_55_out, or_63_out, _0101_out_21);
  or or_56 (or_56_out, or_64_out, _0101_out_22);
  or or_57 (or_57_out, or_65_out, _0101_out_23);
  or or_58 (or_58_out, or_66_out, _0101_out_24);
  or or_59 (or_59_out, or_67_out, _0101_out_25);
  or or_60 (or_60_out, or_68_out, _0101_out_26);
  or or_61 (or_61_out, or_69_out, _0101_out_27);
  or or_62 (or_62_out, or_70_out, _0101_out_28);
  not not_26 (not_26_out, Address_register_out_9);
  register__8_bit _0101 (
    .in_6(and_25_out), .in_7(and_26_out), .in_8(and_27_out), .in_9(and_28_out), .in_10(and_29_out),
    .in_11(and_30_out), .in_12(and_31_out), .in_13(and_32_out), .out_21(_0101_out_21), .out_22(_0101_out_22),
    .out_23(_0101_out_23), .out_24(_0101_out_24), .out_25(_0101_out_25), .out_26(_0101_out_26),
    .out_27(_0101_out_27), .out_28(_0101_out_28), .in_1(d_ff_5_q), .W_R(read_write_q), .Address(and_38_out),
    .RESET(RESET_RAM), .in_3(Program), .in_4(Program), .in_5(Program), .in_14(Program), .in_15(Program),
    .in_17(Program));  // open: in_2, in_16
  and and_38 (and_38_out, not_26_out, not_27_out, Address_register_out_10, Address_register_out_12);
  not not_27 (not_27_out, Address_register_out_11);
  or or_63 (or_63_out, _0110_out_21, or_71_out);
  or or_64 (or_64_out, _0110_out_22, or_72_out);
  or or_65 (or_65_out, _0110_out_23, or_73_out);
  or or_66 (or_66_out, _0110_out_24, or_74_out);
  or or_67 (or_67_out, _0110_out_25, or_75_out);
  or or_68 (or_68_out, _0110_out_26, or_76_out);
  or or_69 (or_69_out, _0110_out_27, or_77_out);
  or or_70 (or_70_out, _0110_out_28, or_78_out);
  not not_28 (not_28_out, Address_register_out_12);
  not not_29 (not_29_out, Address_register_out_9);
  register__8_bit _0110 (
    .in_6(and_25_out), .in_7(and_26_out), .in_8(and_27_out), .in_9(and_28_out), .in_10(and_29_out),
    .in_11(and_30_out), .in_12(and_31_out), .in_13(and_32_out), .out_21(_0110_out_21), .out_22(_0110_out_22),
    .out_23(_0110_out_23), .out_24(_0110_out_24), .out_25(_0110_out_25), .out_26(_0110_out_26),
    .out_27(_0110_out_27), .out_28(_0110_out_28), .in_1(d_ff_5_q), .W_R(read_write_q), .Address(and_39_out),
    .RESET(RESET_RAM), .in_5(Program), .in_16(Program), .in_17(Program));  // open: in_2, in_3, in_4, in_14, in_15
  and and_39 (and_39_out, not_29_out, not_28_out, Address_register_out_10, Address_register_out_11);
  or or_71 (or_71_out, or_79_out, _0111_out_21);
  or or_72 (or_72_out, or_80_out, _0111_out_22);
  or or_73 (or_73_out, or_81_out, _0111_out_23);
  or or_74 (or_74_out, or_82_out, _0111_out_24);
  or or_75 (or_75_out, or_83_out, _0111_out_25);
  or or_76 (or_76_out, or_84_out, _0111_out_26);
  or or_77 (or_77_out, or_85_out, _0111_out_27);
  or or_78 (or_78_out, or_86_out, _0111_out_28);
  and and_40 (and_40_out, Address_register_out_10, Address_register_out_11, Address_register_out_12, not_30_out);
  register__8_bit _0111 (
    .in_6(and_25_out), .in_7(and_26_out), .in_8(and_27_out), .in_9(and_28_out), .in_10(and_29_out),
    .in_11(and_30_out), .in_12(and_31_out), .in_13(and_32_out), .out_21(_0111_out_21), .out_22(_0111_out_22),
    .out_23(_0111_out_23), .out_24(_0111_out_24), .out_25(_0111_out_25), .out_26(_0111_out_26),
    .out_27(_0111_out_27), .out_28(_0111_out_28), .in_1(d_ff_5_q), .W_R(read_write_q), .Address(and_40_out),
    .RESET(RESET_RAM), .in_3(Program), .in_5(Program), .in_14(Program), .in_16(Program), .in_17(Program));  // open: in_2, in_4, in_15
  not not_30 (not_30_out, Address_register_out_9);
  or or_79 (or_79_out, _1000_out_21, or_87_out);
  or or_80 (or_80_out, _1000_out_22, or_88_out);
  or or_81 (or_81_out, _1000_out_23, or_89_out);
  or or_82 (or_82_out, _1000_out_24, or_90_out);
  or or_83 (or_83_out, _1000_out_25, or_91_out);
  or or_84 (or_84_out, _1000_out_26, or_92_out);
  or or_85 (or_85_out, _1000_out_27, or_93_out);
  or or_86 (or_86_out, _1000_out_28, or_94_out);
  and and_41 (and_41_out, not_32_out, not_31_out, not_33_out, Address_register_out_9);
  not not_31 (not_31_out, Address_register_out_11);
  not not_32 (not_32_out, Address_register_out_10);
  not not_33 (not_33_out, Address_register_out_12);
  register__8_bit _1000 (
    .in_6(and_25_out), .in_7(and_26_out), .in_8(and_27_out), .in_9(and_28_out), .in_10(and_29_out),
    .in_11(and_30_out), .in_12(and_31_out), .in_13(and_32_out), .out_21(_1000_out_21), .out_22(_1000_out_22),
    .out_23(_1000_out_23), .out_24(_1000_out_24), .out_25(_1000_out_25), .out_26(_1000_out_26),
    .out_27(_1000_out_27), .out_28(_1000_out_28), .in_1(d_ff_5_q), .W_R(read_write_q), .Address(and_41_out),
    .RESET(RESET_RAM), .in_3(Program), .in_5(Program), .in_14(Program));  // open: in_2, in_4, in_15, in_16, in_17
  or or_87 (or_87_out, or_95_out, _1001_out_21);
  or or_88 (or_88_out, or_96_out, _1001_out_22);
  or or_89 (or_89_out, or_97_out, _1001_out_23);
  or or_90 (or_90_out, or_98_out, _1001_out_24);
  or or_91 (or_91_out, or_99_out, _1001_out_25);
  or or_92 (or_92_out, or_100_out, _1001_out_26);
  or or_93 (or_93_out, or_101_out, _1001_out_27);
  or or_94 (or_94_out, or_102_out, _1001_out_28);
  and and_42 (and_42_out, not_34_out, not_35_out, Address_register_out_9, Address_register_out_12);
  not not_34 (not_34_out, Address_register_out_10);
  not not_35 (not_35_out, Address_register_out_11);
  register__8_bit _1001 (
    .in_6(and_25_out), .in_7(and_26_out), .in_8(and_27_out), .in_9(and_28_out), .in_10(and_29_out),
    .in_11(and_30_out), .in_12(and_31_out), .in_13(and_32_out), .out_21(_1001_out_21), .out_22(_1001_out_22),
    .out_23(_1001_out_23), .out_24(_1001_out_24), .out_25(_1001_out_25), .out_26(_1001_out_26),
    .out_27(_1001_out_27), .out_28(_1001_out_28), .in_1(d_ff_5_q), .W_R(read_write_q), .Address(and_42_out),
    .RESET(RESET_RAM), .in_4(Program), .in_16(Program));  // open: in_2, in_3, in_5, in_14, in_15, in_17
  or or_95 (or_95_out, _1010_out_21, or_103_out);
  or or_96 (or_96_out, _1010_out_22, or_104_out);
  or or_97 (or_97_out, _1010_out_23, or_105_out);
  or or_98 (or_98_out, _1010_out_24, or_106_out);
  or or_99 (or_99_out, _1010_out_25, or_107_out);
  or or_100 (or_100_out, _1010_out_26, or_108_out);
  or or_101 (or_101_out, _1010_out_27, or_109_out);
  or or_102 (or_102_out, _1010_out_28, or_110_out);
  and and_43 (and_43_out, not_36_out, not_37_out, Address_register_out_9, Address_register_out_11);
  not not_36 (not_36_out, Address_register_out_10);
  not not_37 (not_37_out, Address_register_out_12);
  register__8_bit _1010 (
    .in_6(and_25_out), .in_7(and_26_out), .in_8(and_27_out), .in_9(and_28_out), .in_10(and_29_out),
    .in_11(and_30_out), .in_12(and_31_out), .in_13(and_32_out), .out_21(_1010_out_21), .out_22(_1010_out_22),
    .out_23(_1010_out_23), .out_24(_1010_out_24), .out_25(_1010_out_25), .out_26(_1010_out_26),
    .out_27(_1010_out_27), .out_28(_1010_out_28), .in_1(d_ff_5_q), .W_R(read_write_q), .Address(and_43_out),
    .RESET(RESET_RAM), .in_3(Program), .in_4(Program), .in_5(Program), .in_14(Program), .in_16(Program),
    .in_17(Program));  // open: in_2, in_15
  or or_103 (or_103_out, or_111_out, _1011_out_21);
  or or_104 (or_104_out, or_112_out, _1011_out_22);
  or or_105 (or_105_out, or_113_out, _1011_out_23);
  or or_106 (or_106_out, or_114_out, _1011_out_24);
  or or_107 (or_107_out, or_115_out, _1011_out_25);
  or or_108 (or_108_out, or_116_out, _1011_out_26);
  or or_109 (or_109_out, or_117_out, _1011_out_27);
  or or_110 (or_110_out, or_118_out, _1011_out_28);
  and and_44 (and_44_out, Address_register_out_9, Address_register_out_11, Address_register_out_12, not_38_out);
  not not_38 (not_38_out, Address_register_out_10);
  register__8_bit _1011 (
    .in_6(and_25_out), .in_7(and_26_out), .in_8(and_27_out), .in_9(and_28_out), .in_10(and_29_out),
    .in_11(and_30_out), .in_12(and_31_out), .in_13(and_32_out), .out_21(_1011_out_21), .out_22(_1011_out_22),
    .out_23(_1011_out_23), .out_24(_1011_out_24), .out_25(_1011_out_25), .out_26(_1011_out_26),
    .out_27(_1011_out_27), .out_28(_1011_out_28), .in_1(d_ff_5_q), .W_R(read_write_q), .Address(and_44_out),
    .RESET(RESET_RAM), .in_2(Program), .in_16(Program), .in_17(Program));  // open: in_3, in_4, in_5, in_14, in_15
  or or_111 (or_111_out, _1100_out_21, or_119_out);
  or or_112 (or_112_out, _1100_out_22, or_120_out);
  or or_113 (or_113_out, _1100_out_23, or_121_out);
  or or_114 (or_114_out, _1100_out_24, or_122_out);
  or or_115 (or_115_out, _1100_out_25, or_123_out);
  or or_116 (or_116_out, _1100_out_26, or_124_out);
  or or_117 (or_117_out, _1100_out_27, or_125_out);
  or or_118 (or_118_out, _1100_out_28, or_126_out);
  register__8_bit _1100 (
    .in_6(and_25_out), .in_7(and_26_out), .in_8(and_27_out), .in_9(and_28_out), .in_10(and_29_out),
    .in_11(and_30_out), .in_12(and_31_out), .in_13(and_32_out), .out_21(_1100_out_21), .out_22(_1100_out_22),
    .out_23(_1100_out_23), .out_24(_1100_out_24), .out_25(_1100_out_25), .out_26(_1100_out_26),
    .out_27(_1100_out_27), .out_28(_1100_out_28), .in_1(d_ff_5_q), .W_R(read_write_q), .Address(and_45_out),
    .RESET(RESET_RAM), .in_17(Program));  // open: in_2, in_3, in_4, in_5, in_14, in_15, in_16
  and and_45 (and_45_out, not_40_out, not_39_out, Address_register_out_9, Address_register_out_10);
  not not_39 (not_39_out, Address_register_out_12);
  not not_40 (not_40_out, Address_register_out_11);
  or or_119 (or_119_out, or_127_out, _1101_out_21);
  or or_120 (or_120_out, or_128_out, _1101_out_22);
  or or_121 (or_121_out, or_129_out, _1101_out_23);
  or or_122 (or_122_out, or_130_out, _1101_out_24);
  or or_123 (or_123_out, or_131_out, _1101_out_25);
  or or_124 (or_124_out, or_132_out, _1101_out_26);
  or or_125 (or_125_out, or_133_out, _1101_out_27);
  or or_126 (or_126_out, or_134_out, _1101_out_28);
  register__8_bit _1101 (
    .in_6(and_25_out), .in_7(and_26_out), .in_8(and_27_out), .in_9(and_28_out), .in_10(and_29_out),
    .in_11(and_30_out), .in_12(and_31_out), .in_13(and_32_out), .out_21(_1101_out_21), .out_22(_1101_out_22),
    .out_23(_1101_out_23), .out_24(_1101_out_24), .out_25(_1101_out_25), .out_26(_1101_out_26),
    .out_27(_1101_out_27), .out_28(_1101_out_28), .in_1(d_ff_5_q), .W_R(read_write_q), .Address(and_46_out),
    .RESET(RESET_RAM));  // open: in_2, in_3, in_4, in_5, in_14, in_15, in_16, in_17
  and and_46 (and_46_out, Address_register_out_9, Address_register_out_10, Address_register_out_12, not_41_out);
  not not_41 (not_41_out, Address_register_out_11);
  or or_127 (or_127_out, _1110_out_21, _1111_out_21);
  or or_128 (or_128_out, _1110_out_22, _1111_out_22);
  or or_129 (or_129_out, _1110_out_23, _1111_out_23);
  or or_130 (or_130_out, _1110_out_24, _1111_out_24);
  or or_131 (or_131_out, _1110_out_25, _1111_out_25);
  or or_132 (or_132_out, _1110_out_26, _1111_out_26);
  or or_133 (or_133_out, _1110_out_27, _1111_out_27);
  or or_134 (or_134_out, _1110_out_28, _1111_out_28);
  register__8_bit _1110 (
    .in_6(and_25_out), .in_7(and_26_out), .in_8(and_27_out), .in_9(and_28_out), .in_10(and_29_out),
    .in_11(and_30_out), .in_12(and_31_out), .in_13(and_32_out), .out_21(_1110_out_21), .out_22(_1110_out_22),
    .out_23(_1110_out_23), .out_24(_1110_out_24), .out_25(_1110_out_25), .out_26(_1110_out_26),
    .out_27(_1110_out_27), .out_28(_1110_out_28), .in_1(d_ff_5_q), .W_R(read_write_q), .Address(and_47_out),
    .RESET(RESET_RAM));  // open: in_2, in_3, in_4, in_5, in_14, in_15, in_16, in_17
  and and_47 (and_47_out, Address_register_out_9, Address_register_out_10, Address_register_out_11, not_42_out);
  not not_42 (not_42_out, Address_register_out_12);
  and and_48 (and_48_out, Address_register_out_9, Address_register_out_10, Address_register_out_11, Address_register_out_12);
  register__8_bit _1111 (
    .in_6(and_25_out), .in_7(and_26_out), .in_8(and_27_out), .in_9(and_28_out), .in_10(and_29_out),
    .in_11(and_30_out), .in_12(and_31_out), .in_13(and_32_out), .out_21(_1111_out_21), .out_22(_1111_out_22),
    .out_23(_1111_out_23), .out_24(_1111_out_24), .out_25(_1111_out_25), .out_26(_1111_out_26),
    .out_27(_1111_out_27), .out_28(_1111_out_28), .in_1(d_ff_5_q), .W_R(read_write_q), .Address(and_48_out),
    .RESET(RESET_RAM), .in_2(in_7), .in_3(in_9), .in_4(in_11), .in_5(in_13), .in_14(in_15), .in_15(in_17),
    .in_16(in_19), .in_17(in_21));

  // Notes on the sheet:
  //   Writing mode 
  //   to CU: end of LD or STR
  //   0
  //   1
  //   2
  //   3
  //   4
  //   5
  //   6
  //   7
  //   8
  //   9
  //   10
  //   11
  //   12
  //   13
  //   14
  //   15
endmodule

module register__8_bit (
  input  in_1,
  input  in_2,
  input  in_3,
  input  in_4,
  input  in_5,
  input  in_6,
  input  in_7,
  input  in_8,
  input  in_9,
  input  in_10,
  input  in_11,
  input  in_12,
  input  in_13,
  input  in_14,
  input  in_15,
  input  in_16,
  input  in_17,
  input  Address,
  input  W_R,
  input  RESET,
  output out_21,
  output out_22,
  output out_23,
  output out_24,
  output out_25,
  output out_26,
  output out_27,
  output out_28
);

  wire and_1_out, and_2_out, and_3_out, and_4_out, and_5_out, and_6_out, and_7_out, and_8_out, and_9_out,
       and_10_out, and_11_out, and_12_out, and_13_out, and_14_out, and_15_out, and_16_out, and_17_out,
       and_26_out, not_1_out, not_2_out, not_3_out, not_4_out, not_5_out, not_6_out, not_7_out, not_8_out,
       not_9_out, s_r_ff_1_q, s_r_ff_2_q, s_r_ff_3_q, s_r_ff_4_q, s_r_ff_5_q, s_r_ff_6_q, s_r_ff_7_q,
       s_r_ff_8_q;

  not not_1 (not_1_out, in_6);
  not not_2 (not_2_out, in_7);
  not not_3 (not_3_out, in_8);
  not not_4 (not_4_out, in_9);
  not not_5 (not_5_out, in_10);
  not not_6 (not_6_out, in_11);
  not not_7 (not_7_out, in_12);
  not not_8 (not_8_out, in_13);
  and and_1 (and_1_out, and_9_out, in_6);
  and and_2 (and_2_out, and_9_out, in_7);
  and and_3 (and_3_out, and_9_out, in_8);
  and and_4 (and_4_out, and_9_out, in_9);
  and and_5 (and_5_out, and_9_out, in_10);
  and and_6 (and_6_out, and_9_out, in_11);
  and and_7 (and_7_out, and_9_out, in_12);
  and and_8 (and_8_out, and_9_out, in_13);
  and and_9 (and_9_out, Address, W_R);
  and and_10 (and_10_out, and_9_out, not_1_out);
  and and_11 (and_11_out, and_9_out, not_2_out);
  and and_12 (and_12_out, and_9_out, not_3_out);
  and and_13 (and_13_out, and_9_out, not_4_out);
  and and_14 (and_14_out, and_9_out, not_5_out);
  and and_15 (and_15_out, and_9_out, not_6_out);
  and and_16 (and_16_out, and_9_out, not_7_out);
  and and_17 (and_17_out, and_9_out, not_8_out);
  and and_18 (out_21, and_26_out, s_r_ff_1_q);
  S_R_Flip_Flop s_r_ff_1 (
    .S(and_1_out), .clk(in_1), .R(and_10_out), .Q(s_r_ff_1_q), .preset(in_2), .reset(RESET));  // open: Qn, en
  and and_19 (out_22, and_26_out, s_r_ff_2_q);
  S_R_Flip_Flop s_r_ff_2 (
    .S(and_2_out), .clk(in_1), .R(and_11_out), .Q(s_r_ff_2_q), .preset(in_3), .reset(RESET));  // open: Qn, en
  and and_20 (out_23, and_26_out, s_r_ff_3_q);
  S_R_Flip_Flop s_r_ff_3 (
    .S(and_3_out), .clk(in_1), .R(and_12_out), .Q(s_r_ff_3_q), .preset(in_4), .reset(RESET));  // open: Qn, en
  and and_21 (out_24, and_26_out, s_r_ff_4_q);
  S_R_Flip_Flop s_r_ff_4 (
    .S(and_4_out), .clk(in_1), .R(and_13_out), .Q(s_r_ff_4_q), .preset(in_5), .reset(RESET));  // open: Qn, en
  and and_22 (out_25, and_26_out, s_r_ff_5_q);
  S_R_Flip_Flop s_r_ff_5 (
    .S(and_5_out), .clk(in_1), .R(and_14_out), .Q(s_r_ff_5_q), .preset(in_14), .reset(RESET));  // open: Qn, en
  and and_23 (out_26, and_26_out, s_r_ff_6_q);
  S_R_Flip_Flop s_r_ff_6 (
    .S(and_6_out), .clk(in_1), .R(and_15_out), .Q(s_r_ff_6_q), .preset(in_15), .reset(RESET));  // open: Qn, en
  and and_24 (out_27, and_26_out, s_r_ff_7_q);
  S_R_Flip_Flop s_r_ff_7 (
    .S(and_7_out), .clk(in_1), .R(and_16_out), .Q(s_r_ff_7_q), .preset(in_16), .reset(RESET));  // open: Qn, en
  and and_25 (out_28, and_26_out, s_r_ff_8_q);
  S_R_Flip_Flop s_r_ff_8 (
    .S(and_8_out), .clk(in_1), .R(and_17_out), .Q(s_r_ff_8_q), .preset(in_17), .reset(RESET));  // open: Qn, en
  and and_26 (and_26_out, Address, not_9_out);
  not not_9 (not_9_out, W_R);
endmodule

module register__4_bits (
  input  in_1,
  input  in_2,
  input  in_3,
  input  in_4,
  input  in_5,
  input  in_6,
  input  Address,
  input  W_R,
  output out_9,
  output out_10,
  output out_11,
  output out_12
);

  wire and_1_out, and_2_out, and_3_out, and_4_out, and_5_out, and_6_out, and_7_out, and_8_out, and_9_out,
       and_14_out, not_1_out, not_2_out, not_3_out, not_4_out, not_5_out, s_r_ff_1_q, s_r_ff_2_q, s_r_ff_3_q,
       s_r_ff_4_q;

  not not_1 (not_1_out, in_2);
  not not_2 (not_2_out, in_3);
  not not_3 (not_3_out, in_4);
  not not_4 (not_4_out, in_5);
  and and_1 (and_1_out, and_5_out, in_2);
  and and_2 (and_2_out, and_5_out, in_3);
  and and_3 (and_3_out, and_5_out, in_4);
  and and_4 (and_4_out, and_5_out, in_5);
  and and_5 (and_5_out, Address, W_R);
  S_R_Flip_Flop s_r_ff_1 (
    .S(and_1_out), .clk(in_1), .R(and_6_out), .Q(s_r_ff_1_q), .reset(in_6));  // open: Qn, preset, en
  and and_6 (and_6_out, and_5_out, not_1_out);
  S_R_Flip_Flop s_r_ff_2 (
    .S(and_2_out), .clk(in_1), .R(and_7_out), .Q(s_r_ff_2_q), .reset(in_6));  // open: Qn, preset, en
  and and_7 (and_7_out, and_5_out, not_2_out);
  S_R_Flip_Flop s_r_ff_3 (
    .S(and_3_out), .clk(in_1), .R(and_8_out), .Q(s_r_ff_3_q), .reset(in_6));  // open: Qn, preset, en
  and and_8 (and_8_out, and_5_out, not_3_out);
  S_R_Flip_Flop s_r_ff_4 (
    .S(and_4_out), .clk(in_1), .R(and_9_out), .Q(s_r_ff_4_q), .reset(in_6));  // open: Qn, preset, en
  and and_9 (and_9_out, and_5_out, not_4_out);
  and and_10 (out_9, and_14_out, s_r_ff_1_q);
  and and_11 (out_10, and_14_out, s_r_ff_2_q);
  and and_12 (out_11, and_14_out, s_r_ff_3_q);
  and and_13 (out_12, and_14_out, s_r_ff_4_q);
  and and_14 (and_14_out, Address, not_5_out);
  not not_5 (not_5_out, W_R);
endmodule

// BUS gate status
module IR (
  input  CLK,
  input  in_2,
  input  from_RAM,
  input  BZ_done,
  input  RESET,
  input  in_6,
  input  in_7,
  input  in_8,
  input  in_9,
  input  in_10,
  input  in_11,
  input  in_12,
  input  in_13,
  input  in_14,
  input  ALU_back,
  input  in_16,
  input  ZERO,
  output out_18,
  output out_19,
  output out_20,
  output ADDRESS,
  output R_W,
  output Tick,
  output reset_MBR,
  output ALU_R_R_W,
  output ALU_CU,
  output reset_ALU,
  output N_L,
  output PRT,
  output RAM_R_W,
  output INP,
  output to_RAM,
  output MAR_MBR_R_W,
  output HALT,
  output L_R,
  output out_36,
  output adress,
  output out_38,
  output out_39,
  output out_40,
  output BZ
);

  wire ADD_out, and_1_out, and_3_out, and_4_out, and_5_out, and_6_out, and_7_out, and_8_out, and_9_out,
       and_10_out, and_11_out, and_12_out, and_13_out, and_15_out, and_16_out, and_17_out, and_18_out,
       and_19_out, and_21_out, and_23_out, and_26_out, and_27_out, and_30_out, and_31_out, BZ_out, COMP_out,
       d_ff_1_q, d_ff_2_q, d_ff_3_q, d_ff_4_q, d_ff_5_q, d_ff_6_q, d_ff_7_q, d_ff_8_q, d_ff_9_q, d_ff_10_q,
       d_ff_11_q, d_ff_12_q, d_ff_13_q, d_ff_14_q, d_ff_15_q, d_ff_16_q, d_ff_17_q, demultiplexer_1_out0,
       demultiplexer_1_out1, HALT_out, INP_out, IR_out_21, IR_out_22, IR_out_23, IR_out_24, IR_out_25,
       IR_out_26, IR_out_27, IR_out_28, LD_out, LD_status_q, MBR_status_q, multiplexer_1_out,
       multiplexer_2_out, multiplexer_3_out, multiplexer_4_out, multiplexer_5_out, multiplexer_6_out,
       not_1_out, not_2_out, not_3_out, not_4_out, not_5_out, not_6_out, not_7_out, not_8_out, not_9_out,
       not_10_out, not_11_out, not_12_out, not_13_out, not_14_out, not_15_out, not_16_out, not_17_out,
       not_18_out, not_19_out, not_20_out, not_21_out, not_22_out, not_23_out, not_24_out, not_25_out,
       not_26_out, not_27_out, not_28_out, not_29_out, not_30_out, not_31_out, not_32_out, not_33_out,
       or_1_out, or_2_out, or_3_out, or_4_out, or_5_out, or_6_out, or_7_out, or_8_out, or_9_out, or_11_out,
       or_12_out, or_13_out, or_14_out, or_15_out, or_16_out, or_17_out, or_19_out, or_20_out, or_22_out,
       or_23_out, or_25_out, or_26_out, or_31_out, or_32_out, PRT_out, R1_q, R2_q, Register_status_q,
       Register_status_qn, STOP_out, SUB_out;

  or or_1 (or_1_out, and_13_out, and_26_out);
  not not_1 (not_1_out, CLK);
  or or_2 (or_2_out, or_1_out, BZ_done);
  or or_3 (or_3_out, demultiplexer_1_out0, and_5_out);
  Demultiplexer demultiplexer_1 (
    .out0(demultiplexer_1_out0), .out1(demultiplexer_1_out1), .in(from_RAM), .sel(LD_out), .en(in_14));
  or or_4 (or_4_out, or_5_out, d_ff_3_q);
  D_Flip_Flop End_of_cycle (
    .clk(not_1_out), .D(or_2_out), .Q(out_20), .preset(or_3_out), .reset(RESET));  // open: Qn, en
  or or_5 (or_5_out, out_20, and_3_out, RESET);
  or or_6 (or_6_out, d_ff_1_q, or_9_out);
  D_Flip_Flop d_ff_1 (.Q(d_ff_1_q), .preset(in_2), .reset(or_4_out));  // open: clk, D, Qn, en
  or or_7 (or_7_out, BZ_done, and_5_out);
  not not_2 (not_2_out, BZ_out);
  and and_1 (and_1_out, not_2_out, in_16);
  not not_3 (not_3_out, ZERO);
  and and_2 (BZ, BZ_out, ZERO);
  not not_4 (not_4_out, CLK);
  D_Flip_Flop d_ff_2 (.clk(CLK), .D(d_ff_1_q), .Q(d_ff_2_q), .reset(or_5_out));  // open: Qn, preset, en
  D_Flip_Flop LD_status (.Q(LD_status_q), .preset(demultiplexer_1_out1), .reset(not_21_out));  // open: clk, D, Qn, en
  and and_3 (and_3_out, d_ff_4_q, STOP_out);
  register__8_bit IR (
    .in_6(in_6), .in_7(in_7), .in_8(in_8), .in_9(in_9), .in_10(in_10), .in_11(in_11), .in_12(in_12),
    .in_13(in_13), .out_21(IR_out_21), .out_22(IR_out_22), .out_23(IR_out_23), .out_24(IR_out_24),
    .out_25(IR_out_25), .out_26(IR_out_26), .out_27(IR_out_27), .out_28(IR_out_28), .in_1(d_ff_2_q),
    .W_R(d_ff_1_q), .Address(in_14), .RESET(or_5_out));  // open: in_2, in_3, in_4, in_5, in_14, in_15, in_16, in_17
  and and_4 (and_4_out, BZ_out, reset_MBR);
  and and_5 (and_5_out, CLK, in_16, not_3_out, BZ_out);
  not not_5 (not_5_out, not_4_out);
  D_Flip_Flop d_ff_3 (.clk(not_4_out), .D(d_ff_2_q), .Q(d_ff_3_q), .reset(or_5_out));  // open: Qn, preset, en
  and and_6 (and_6_out, LD_out, d_ff_13_q);
  or or_8 (or_8_out, INP_out, RAM_R_W, LD_out);
  and u_BZ (BZ_out, IR_out_21, not_7_out);
  not not_6 (not_6_out, IR_out_21);
  not not_7 (not_7_out, IR_out_22);
  not not_8 (not_8_out, IR_out_23);
  not not_9 (not_9_out, IR_out_24);
  not not_10 (not_10_out, IR_out_25);
  not not_11 (not_11_out, IR_out_26);
  not not_12 (not_12_out, IR_out_27);
  not not_13 (not_13_out, IR_out_28);
  not not_14 (not_14_out, not_5_out);
  D_Flip_Flop d_ff_4 (.clk(not_5_out), .D(d_ff_3_q), .Q(d_ff_4_q), .reset(or_5_out));  // open: Qn, preset, en
  Multiplexer multiplexer_1 (.in0(d_ff_4_q), .in1(d_ff_5_q), .out(multiplexer_1_out), .sel(or_11_out), .en(in_14));
  or or_9 (or_9_out, and_7_out, demultiplexer_1_out1, and_6_out);
  not not_15 (not_15_out, LD_status_q);
  or or_10 (reset_MBR, d_ff_3_q, or_5_out);
  and and_7 (and_7_out, not_17_out, INP_out, d_ff_6_q);
  or or_11 (or_11_out, PRT_out, RAM_R_W);
  and LD (LD_out, not_6_out, IR_out_22, not_8_out);
  and STR (RAM_R_W, not_6_out, IR_out_22, IR_out_23);
  D_Flip_Flop Register_status (
    .Q(Register_status_q), .Qn(Register_status_qn), .preset(or_12_out), .reset(or_13_out));  // open: clk, D, en
  or or_12 (or_12_out, COMP_out, or_8_out, ALU_back);
  or or_13 (or_13_out, or_5_out, and_4_out, and_1_out);
  S_R_Flip_Flop R1 (.S(IR_out_27), .clk(d_ff_4_q), .R(not_12_out), .Q(R1_q), .reset(or_5_out));  // open: Qn, preset, en
  S_R_Flip_Flop R2 (.S(IR_out_28), .clk(d_ff_4_q), .R(not_13_out), .Q(R2_q), .reset(or_5_out));  // open: Qn, preset, en
  not not_16 (not_16_out, not_14_out);
  D_Flip_Flop d_ff_5 (.clk(not_14_out), .D(d_ff_4_q), .Q(d_ff_5_q), .reset(or_5_out));  // open: Qn, preset, en
  not not_17 (not_17_out, d_ff_5_q);
  and and_8 (and_8_out, LD_status_q, d_ff_11_q);
  or or_14 (or_14_out, and_8_out, d_ff_6_q);
  and ADD (ADD_out, not_6_out, not_7_out, IR_out_23, not_9_out, not_10_out, not_11_out);
  not not_18 (not_18_out, Register_status_q);
  not not_19 (not_19_out, multiplexer_2_out);
  and and_9 (and_9_out, not_19_out, R1_q);
  and and_10 (and_10_out, R2_q, multiplexer_2_out);
  not not_20 (not_20_out, not_16_out);
  D_Flip_Flop d_ff_6 (.clk(not_16_out), .D(d_ff_5_q), .Q(d_ff_6_q), .reset(or_5_out));  // open: Qn, preset, en
  or or_15 (or_15_out, and_11_out, and_12_out);
  and and_11 (and_11_out, multiplexer_1_out, or_16_out);
  and and_12 (and_12_out, not_21_out, ALU_back);
  not not_21 (not_21_out, d_ff_15_q);
  or or_16 (or_16_out, or_17_out, or_11_out, ADD_out, COMP_out);
  or or_17 (or_17_out, BZ_out, SUB_out);
  and SUB (SUB_out, not_6_out, not_7_out, IR_out_23, not_9_out, not_10_out, IR_out_26);
  Multiplexer multiplexer_2 (
    .in0(Register_status_q), .in1(not_18_out), .out(multiplexer_2_out), .sel(and_19_out), .en(in_14));
  or or_18 (out_38, and_9_out, and_10_out);
  and and_13 (and_13_out, d_ff_8_q, PRT_out, d_ff_9_q);
  D_Flip_Flop d_ff_7 (.Q(d_ff_7_q), .preset(or_15_out), .reset(or_19_out));  // open: clk, D, Qn, en
  or or_19 (or_19_out, or_5_out, d_ff_9_q);
  not not_22 (not_22_out, PRT_out);
  and and_14 (ALU_CU, ALU_back, not_22_out, d_ff_17_q);
  // AND_Gate MULT has open pins: in0=not_6_out, in1=not_7_out, in2=IR_out_23, in3=not_9_out, in4=IR_out_25, in5=not_11_out, out=open
  not not_23 (not_23_out, not_20_out);
  D_Flip_Flop d_ff_8 (.clk(not_20_out), .D(d_ff_7_q), .Q(d_ff_8_q), .reset(or_5_out));  // open: Qn, preset, en
  and and_15 (and_15_out, d_ff_17_q, d_ff_6_q, LD_out);
  not not_24 (not_24_out, d_ff_5_q);
  and and_16 (and_16_out, not_24_out, and_15_out);
  and and_17 (and_17_out, d_ff_5_q, INP_out);
  and and_18 (and_18_out, or_14_out, LD_out);
  and u_INP (INP_out, not_6_out, not_7_out, not_8_out, IR_out_24, not_10_out, not_11_out, not_12_out);
  D_Flip_Flop d_ff_9 (.clk(not_23_out), .D(d_ff_8_q), .Q(d_ff_9_q), .reset(or_5_out));  // open: Qn, preset, en
  or or_20 (or_20_out, or_9_out, and_1_out);
  and and_19 (and_19_out, R_W, COMP_out);
  and and_20 (INP, INP_out, multiplexer_1_out);
  or or_21 (MAR_MBR_R_W, and_18_out, INP, and_21_out);
  and and_21 (and_21_out, d_ff_7_q, or_11_out);
  and u_PRT (PRT_out, not_6_out, not_7_out, not_8_out, IR_out_24, not_10_out, not_11_out, IR_out_27);
  D_Flip_Flop d_ff_10 (.Q(d_ff_10_q), .preset(or_20_out), .reset(or_22_out));  // open: clk, D, Qn, en
  or or_22 (or_22_out, or_5_out, d_ff_12_q);
  and COMP (COMP_out, not_6_out, not_7_out, not_8_out, IR_out_24, not_10_out, IR_out_26, not_12_out);
  Multiplexer multiplexer_3 (.in0(IR_out_26), .in1(IR_out_27), .out(multiplexer_3_out), .sel(or_8_out), .en(in_14));
  not not_25 (not_25_out, not_23_out);
  D_Flip_Flop d_ff_11 (.clk(not_23_out), .D(d_ff_10_q), .Q(d_ff_11_q), .reset(or_5_out));  // open: Qn, preset, en
  and and_22 (R_W, d_ff_11_q, not_15_out);
  and STOP (STOP_out, not_6_out, not_7_out, not_8_out, not_9_out);
  Multiplexer multiplexer_4 (.in0(IR_out_25), .in1(IR_out_26), .out(multiplexer_4_out), .sel(or_8_out), .en(in_14));
  not not_26 (not_26_out, not_25_out);
  D_Flip_Flop d_ff_12 (.clk(not_25_out), .D(d_ff_11_q), .Q(d_ff_12_q), .reset(or_5_out));  // open: Qn, preset, en
  D_Flip_Flop d_ff_13 (.clk(not_26_out), .D(and_23_out), .Q(d_ff_13_q), .reset(or_5_out));  // open: Qn, preset, en
  and and_23 (and_23_out, not_28_out, d_ff_12_q);
  or or_23 (or_23_out, d_ff_12_q, and_17_out);
  and and_24 (ALU_R_R_W, d_ff_8_q, not_27_out);
  not not_27 (not_27_out, Register_status_q);
  and and_25 (HALT, d_ff_4_q, HALT_out);
  and u_HALT (HALT_out, IR_out_21, IR_out_22);
  Multiplexer multiplexer_5 (.in0(IR_out_23), .in1(IR_out_24), .out(multiplexer_5_out), .sel(or_8_out), .en(in_14));
  Multiplexer multiplexer_6 (.in0(IR_out_24), .in1(IR_out_25), .out(multiplexer_6_out), .sel(or_8_out), .en(in_14));
  and and_26 (and_26_out, d_ff_13_q, not_15_out);
  or or_24 (reset_ALU, or_7_out, and_26_out);
  not not_28 (not_28_out, BZ_out);
  register__4_bits register_4_bits_1 (
    .in_2(multiplexer_5_out), .in_3(multiplexer_6_out), .in_4(multiplexer_4_out), .in_5(multiplexer_3_out),
    .out_9(out_36), .out_10(adress), .out_11(out_39), .out_12(out_40), .in_1(d_ff_5_q), .Address(in_14),
    .W_R(d_ff_4_q), .in_6(or_5_out));
  or or_25 (or_25_out, and_15_out, INP, or_5_out);
  D_Flip_Flop d_ff_14 (.Q(d_ff_14_q), .preset(multiplexer_2_out), .reset(or_26_out));  // open: clk, D, Qn, en
  or or_26 (or_26_out, or_5_out, and_6_out, Register_status_qn);
  and and_27 (and_27_out, d_ff_9_q, RAM_R_W);
  not not_29 (not_29_out, not_26_out);
  D_Flip_Flop d_ff_15 (.clk(not_26_out), .D(d_ff_14_q), .Q(d_ff_15_q), .reset(or_5_out));  // open: Qn, preset, en
  or or_27 (ADDRESS, d_ff_7_q, d_ff_9_q, R_W);
  or or_28 (Tick, d_ff_8_q, and_15_out, or_23_out);
  or or_29 (to_RAM, and_16_out, and_27_out);
  and and_28 (L_R, d_ff_7_q, not_30_out, multiplexer_2_out);
  not not_30 (not_30_out, or_8_out);
  not not_31 (not_31_out, not_29_out);
  D_Flip_Flop d_ff_16 (.clk(not_29_out), .D(d_ff_15_q), .Q(d_ff_16_q), .reset(or_5_out));  // open: Qn, preset, en
  or or_30 (N_L, or_17_out, COMP_out);
  and and_29 (PRT, PRT_out, d_ff_8_q);
  and and_30 (and_30_out, or_25_out, not_32_out);
  not not_32 (not_32_out, out_20);
  D_Flip_Flop d_ff_17 (.clk(not_31_out), .D(d_ff_16_q), .Q(d_ff_17_q), .reset(or_5_out));  // open: Qn, preset, en
  D_Flip_Flop MBR_status (.Q(MBR_status_q), .preset(d_ff_3_q), .reset(or_31_out));  // open: clk, D, Qn, en
  or or_31 (or_31_out, and_30_out, or_11_out, reset_ALU);
  D_Flip_Flop BUS_gate_status (.Q(out_19), .preset(or_6_out), .reset(or_32_out));  // open: clk, D, Qn, en
  or or_32 (or_32_out, and_30_out, and_31_out, reset_ALU);
  and and_31 (and_31_out, d_ff_9_q, or_11_out);
  not not_33 (not_33_out, MBR_status_q);
  and and_32 (out_18, not_33_out, in_14);

  // Notes on the sheet:
  //   010
  //   10
  //   011
  //   001000
  //   001001
  //   001010
  //   0001000
  //   to GR
  //   Load register
  //   0001001
  //   0001010
  //   Save in register
  //   0000
  //   11
endmodule

module digital_display (
  input  CLK,
  input  PRT,
  input  Reset,
  input  in_4,
  input  in_5,
  input  in_6,
  input  in_7,
  input  in_8,
  input  in_9,
  input  in_10,
  input  in_11,
  output out_12,
  output out_13,
  output out_14,
  output out_15,
  output out_16,
  output out_17,
  output out_18,
  output out_19,
  output out_20,
  output out_21,
  output out_22,
  output out_23,
  output out_24,
  output out_25
);

  wire D01_2_out, D01_out, D02_2_out, D02_out, D03_2_out, D03_out, D04_2_out, D04_out, D05_2_out, D05_out,
       D06_2_out, D06_out, D07_2_out, D07_out, D08_2_out, D08_out, D09_2_out, D09_out, D10_2_out, D10_out,
       D11_2_out, D11_out, D12_2_out, D12_out, D13_2_out, D13_out, D14_2_out, D14_out, D15_2_out, D15_out,
       D16_2_out, D16_out, D17_2_out, D17_out, D18_2_out, D18_out, D19_2_out, D19_out, D20_2_out, D20_out,
       D21_2_out, D21_out, D22_2_out, D22_out, D23_2_out, D23_out, D24_2_out, D24_out, D25_2_out, D25_out,
       D26_2_out, D26_out, D27_2_out, D27_out, D28_2_out, D28_out, D29_2_out, D29_out, D30_2_out, D30_out,
       D31_2_out, D31_out, D32_2_out, D32_out, D33_2_out, D33_out, D34_2_out, D34_out, D35_2_out, D35_out,
       D36_2_out, D36_out, D37_2_out, D37_out, D38_2_out, D38_out, d_ff_1_q, d_ff_2_q, d_ff_3_q, d_ff_4_q,
       not_1_out, not_2_out, not_3_out, not_4_out, not_5_out, not_6_out, not_7_out, not_8_out, not_9_out,
       not_10_out, or_1_out, register_8_bit_1_out_21, register_8_bit_1_out_22, register_8_bit_1_out_23,
       register_8_bit_1_out_24, register_8_bit_1_out_25, register_8_bit_1_out_26, register_8_bit_1_out_27,
       register_8_bit_1_out_28;

  D_Flip_Flop d_ff_1 (.Q(d_ff_1_q), .preset(CLK), .reset(Reset));  // open: clk, D, Qn, en
  not not_1 (not_1_out, CLK);
  D_Flip_Flop d_ff_2 (.Q(d_ff_2_q), .preset(PRT), .reset(or_1_out));  // open: clk, D, Qn, en
  or or_1 (or_1_out, Reset, d_ff_4_q);
  register__8_bit register_8_bit_1 (
    .in_6(in_4), .in_7(in_5), .in_8(in_6), .in_9(in_7), .in_10(in_8), .in_11(in_9), .in_12(in_10),
    .in_13(in_11), .out_21(register_8_bit_1_out_21), .out_22(register_8_bit_1_out_22),
    .out_23(register_8_bit_1_out_23), .out_24(register_8_bit_1_out_24), .out_25(register_8_bit_1_out_25),
    .out_26(register_8_bit_1_out_26), .out_27(register_8_bit_1_out_27), .out_28(register_8_bit_1_out_28),
    .in_1(d_ff_3_q), .W_R(d_ff_2_q), .Address(d_ff_1_q), .RESET(Reset));  // open: in_2, in_3, in_4, in_5, in_14, in_15, in_16, in_17
  not not_2 (not_2_out, not_1_out);
  D_Flip_Flop d_ff_3 (.clk(not_1_out), .D(d_ff_2_q), .Q(d_ff_3_q), .reset(Reset));  // open: Qn, preset, en
  not not_3 (not_3_out, register_8_bit_1_out_21);
  not not_4 (not_4_out, register_8_bit_1_out_22);
  not not_5 (not_5_out, register_8_bit_1_out_23);
  not not_6 (not_6_out, register_8_bit_1_out_24);
  not not_7 (not_7_out, register_8_bit_1_out_25);
  not not_8 (not_8_out, register_8_bit_1_out_26);
  not not_9 (not_9_out, register_8_bit_1_out_27);
  not not_10 (not_10_out, register_8_bit_1_out_28);
  D_Flip_Flop d_ff_4 (.clk(not_2_out), .D(d_ff_3_q), .Q(d_ff_4_q), .reset(Reset));  // open: Qn, preset, en
  and D01 (D01_out, not_3_out, register_8_bit_1_out_22, not_5_out);
  and D02 (D02_out, not_4_out, register_8_bit_1_out_23, register_8_bit_1_out_24);
  and D03 (D03_out, register_8_bit_1_out_24, register_8_bit_1_out_21);
  and D04 (D04_out, register_8_bit_1_out_21, not_4_out);
  and D05 (D05_out, not_6_out, register_8_bit_1_out_23);
  and D06 (D06_out, not_3_out, register_8_bit_1_out_22, not_5_out);
  and D07 (D07_out, register_8_bit_1_out_22, register_8_bit_1_out_23, not_6_out);
  and D08 (D08_out, not_5_out, not_6_out);
  and D09 (D09_out, register_8_bit_1_out_21, not_4_out);
  and D10 (D10_out, register_8_bit_1_out_21, register_8_bit_1_out_23);
  and D11 (D11_out, not_4_out, not_5_out, not_6_out);
  and D12 (D12_out, register_8_bit_1_out_21, not_5_out, not_6_out);
  and D13 (D13_out, not_3_out, register_8_bit_1_out_22, register_8_bit_1_out_24);
  and D14 (D14_out, not_3_out, register_8_bit_1_out_23, register_8_bit_1_out_24);
  and D15 (D15_out, register_8_bit_1_out_21, not_4_out, not_5_out);
  and D16 (D16_out, register_8_bit_1_out_22, register_8_bit_1_out_23);
  and D17 (D17_out, register_8_bit_1_out_23, not_6_out);
  and D18 (D18_out, not_3_out, not_5_out, not_6_out);
  and D19 (D19_out, register_8_bit_1_out_21, not_4_out, not_5_out);
  and D20 (D20_out, register_8_bit_1_out_21, not_5_out, register_8_bit_1_out_24);
  and D21 (D21_out, not_3_out, register_8_bit_1_out_23, register_8_bit_1_out_24);
  and D22 (D22_out, not_4_out, register_8_bit_1_out_23, not_6_out);
  and D23 (D23_out, not_3_out, not_4_out);
  and D24 (D24_out, not_4_out, not_5_out, not_6_out);
  and D25 (D25_out, register_8_bit_1_out_23, not_6_out);
  and D26 (D26_out, register_8_bit_1_out_21, register_8_bit_1_out_22);
  and D27 (D27_out, register_8_bit_1_out_21, register_8_bit_1_out_23);
  and D28 (D28_out, not_4_out, not_5_out, not_6_out);
  and D29 (D29_out, register_8_bit_1_out_22, not_5_out, register_8_bit_1_out_24);
  and D30 (D30_out, register_8_bit_1_out_21, not_4_out, register_8_bit_1_out_24);
  and D31 (D31_out, not_3_out, not_4_out, register_8_bit_1_out_23);
  and D32 (D32_out, register_8_bit_1_out_22, register_8_bit_1_out_23, not_6_out);
  and D33 (D33_out, register_8_bit_1_out_21, not_5_out);
  and D34 (D34_out, not_3_out, register_8_bit_1_out_23, register_8_bit_1_out_24);
  and D35 (D35_out, register_8_bit_1_out_21, not_5_out, register_8_bit_1_out_24);
  and D36 (D36_out, not_3_out, register_8_bit_1_out_22);
  and D37 (D37_out, register_8_bit_1_out_21, not_4_out);
  and D38 (D38_out, not_3_out, not_5_out);
  and D01_2 (D01_2_out, not_7_out, register_8_bit_1_out_26, not_9_out);
  and D02_2 (D02_2_out, not_8_out, register_8_bit_1_out_27, register_8_bit_1_out_28);
  and D03_2 (D03_2_out, register_8_bit_1_out_28, register_8_bit_1_out_25);
  and D04_2 (D04_2_out, register_8_bit_1_out_25, not_8_out);
  and D05_2 (D05_2_out, not_10_out, register_8_bit_1_out_27);
  and D06_2 (D06_2_out, not_7_out, register_8_bit_1_out_26, not_9_out);
  and D07_2 (D07_2_out, register_8_bit_1_out_26, register_8_bit_1_out_27, not_10_out);
  and D08_2 (D08_2_out, not_9_out, not_10_out);
  and D09_2 (D09_2_out, register_8_bit_1_out_25, not_8_out);
  and D10_2 (D10_2_out, register_8_bit_1_out_25, register_8_bit_1_out_27);
  and D11_2 (D11_2_out, not_8_out, not_9_out, not_10_out);
  and D12_2 (D12_2_out, register_8_bit_1_out_25, not_9_out, not_10_out);
  and D13_2 (D13_2_out, not_7_out, register_8_bit_1_out_26, register_8_bit_1_out_28);
  and D14_2 (D14_2_out, not_7_out, register_8_bit_1_out_27, register_8_bit_1_out_28);
  and D15_2 (D15_2_out, register_8_bit_1_out_25, not_8_out, not_9_out);
  and D16_2 (D16_2_out, register_8_bit_1_out_26, register_8_bit_1_out_27);
  and D17_2 (D17_2_out, register_8_bit_1_out_27, not_10_out);
  and D18_2 (D18_2_out, not_7_out, not_9_out, not_10_out);
  and D19_2 (D19_2_out, register_8_bit_1_out_25, not_8_out, not_9_out);
  and D20_2 (D20_2_out, register_8_bit_1_out_25, not_9_out, register_8_bit_1_out_28);
  and D21_2 (D21_2_out, not_7_out, register_8_bit_1_out_27, register_8_bit_1_out_28);
  and D22_2 (D22_2_out, not_8_out, register_8_bit_1_out_27, not_10_out);
  and D23_2 (D23_2_out, not_7_out, not_8_out);
  and D24_2 (D24_2_out, not_8_out, not_9_out, not_10_out);
  and D25_2 (D25_2_out, register_8_bit_1_out_27, not_10_out);
  and D26_2 (D26_2_out, register_8_bit_1_out_25, register_8_bit_1_out_26);
  and D27_2 (D27_2_out, register_8_bit_1_out_25, register_8_bit_1_out_27);
  and D28_2 (D28_2_out, not_8_out, not_9_out, not_10_out);
  and D29_2 (D29_2_out, register_8_bit_1_out_26, not_9_out, register_8_bit_1_out_28);
  and D30_2 (D30_2_out, register_8_bit_1_out_25, not_8_out, register_8_bit_1_out_28);
  and D31_2 (D31_2_out, not_7_out, not_8_out, register_8_bit_1_out_27);
  and D32_2 (D32_2_out, register_8_bit_1_out_26, register_8_bit_1_out_27, not_10_out);
  and D33_2 (D33_2_out, register_8_bit_1_out_25, not_9_out);
  and D34_2 (D34_2_out, not_7_out, register_8_bit_1_out_27, register_8_bit_1_out_28);
  and D35_2 (D35_2_out, register_8_bit_1_out_25, not_9_out, register_8_bit_1_out_28);
  and D36_2 (D36_2_out, not_7_out, register_8_bit_1_out_26);
  and D37_2 (D37_2_out, register_8_bit_1_out_25, not_8_out);
  and D38_2 (D38_2_out, not_7_out, not_9_out);
  or or_2 (out_12, D01_out, D02_out, D03_out, D04_out, D05_out);
  or or_3 (out_13, D06_out, D07_out, D08_out, D09_out, D10_out);
  or or_4 (out_14, D11_out, D12_out, D13_out, D14_out, D15_out, D16_out, D17_out);
  or or_5 (out_16, D24_out, D25_out, D26_out, D27_out);
  or or_6 (out_18, D34_out, D35_out, D36_out, D37_out, D38_out);
  or or_7 (out_19, D01_2_out, D02_2_out, D03_2_out, D04_2_out, D05_2_out);
  or or_8 (out_20, D06_2_out, D07_2_out, D08_2_out, D09_2_out, D10_2_out);
  or or_9 (out_15, D18_out, D19_out, D20_out, D21_out, D22_out, D23_out);
  or or_10 (out_17, D28_out, D29_out, D30_out, D31_out, D32_out, D33_out);
  or or_11 (out_21, D11_2_out, D12_2_out, D13_2_out, D14_2_out, D15_2_out, D16_2_out, D17_2_out);
  or or_12 (out_22, D18_2_out, D19_2_out, D20_2_out, D21_2_out, D22_2_out, D23_2_out);
  or or_13 (out_23, D24_2_out, D25_2_out, D26_2_out, D27_2_out);
  or or_14 (out_24, D28_2_out, D29_2_out, D30_2_out, D31_2_out, D32_2_out, D33_2_out);
  or or_15 (out_25, D34_2_out, D35_2_out, D36_2_out, D37_2_out, D38_2_out);
endmodule

module input_buffer (
  input  CLK,
  input  Reset,
  input  in_3,
  input  in_4,
  input  in_5,
  input  in_6,
  input  in_7,
  input  in_8,
  input  in_9,
  input  in_10,
  input  in_11,
  input  in_12,
  input  INP,
  output out_14,
  output out_15,
  output out_16,
  output out_17
);

  wire d_ff_1_q, d_ff_2_qn, not_1_out, or_1_out, or_2_out, or_3_out, or_4_out, or_5_out;

  D_Flip_Flop d_ff_1 (.Q(d_ff_1_q), .preset(CLK), .reset(Reset));  // open: clk, D, Qn, en
  or or_1 (or_1_out, in_9, in_10, in_8, in_7);
  or or_2 (or_2_out, in_5, in_6, in_9, in_10);
  or or_3 (or_3_out, in_11, in_12);
  or or_4 (or_4_out, in_4, in_6, in_8, in_10, in_12);
  register__4_bits register_4_bits_1 (
    .in_2(or_3_out), .in_3(or_1_out), .in_4(or_2_out), .in_5(or_4_out), .out_9(out_14), .out_10(out_15),
    .out_11(out_16), .out_12(out_17), .in_1(CLK), .Address(d_ff_1_q), .W_R(d_ff_2_qn), .in_6(Reset));
  D_Flip_Flop d_ff_2 (.Qn(d_ff_2_qn), .preset(INP), .reset(or_5_out));  // open: clk, D, Q, en
  or or_5 (or_5_out, Reset, not_1_out);
  not not_1 (not_1_out, INP);
endmodule

module clock (
  input  Button_ON_OFF,
  input  Input_form_CU,
  input  BZ,
  input  HALT,
  output Reset,
  output CLK,
  output ON_OFF,
  output BZ_end,
  output out_9,
  output out_10,
  output out_11,
  output out_12,
  output out_13,
  output out_14,
  output out_15
);

  wire and_1_out, clock_1_out, d_ff_3_q, d_ff_4_q, d_ff_5_q, d_ff_6_q, d_ff_7_q, d_ff_8_q, d_ff_10_q,
       d_ff_11_q, d_ff_12_q, d_ff_13_q, not_1_out, not_2_out, not_3_out, not_4_out, not_5_out, not_6_out,
       not_7_out, not_8_out, not_9_out, or_2_out, or_3_out;

  or or_1 (Reset, Button_ON_OFF, HALT);
  and and_1 (and_1_out, Button_ON_OFF, not_1_out);
  D_Flip_Flop d_ff_1 (.Q(ON_OFF), .preset(and_1_out), .reset(HALT));  // open: clk, D, Qn, en
  not not_1 (not_1_out, ON_OFF);
  Clock clock_1 (.out(clock_1_out));
  and and_2 (CLK, ON_OFF, clock_1_out);
  D_Flip_Flop d_ff_2 (.Q(out_15), .preset(or_2_out), .reset(d_ff_5_q));  // open: clk, D, Qn, en
  or or_2 (or_2_out, Button_ON_OFF, Input_form_CU);
  not not_2 (not_2_out, CLK);
  D_Flip_Flop d_ff_3 (.clk(CLK), .D(out_15), .Q(d_ff_3_q), .reset(Button_ON_OFF));  // open: Qn, preset, en
  D_Flip_Flop d_ff_4 (.Q(d_ff_4_q), .preset(BZ), .reset(or_3_out));  // open: clk, D, Qn, en
  or or_3 (or_3_out, Button_ON_OFF, d_ff_8_q);
  D_Flip_Flop d_ff_5 (.clk(not_2_out), .D(d_ff_3_q), .Q(d_ff_5_q), .reset(Button_ON_OFF));  // open: Qn, preset, en
  D_Flip_Flop d_ff_6 (.clk(not_2_out), .D(d_ff_4_q), .Q(d_ff_6_q), .reset(Button_ON_OFF));  // open: Qn, preset, en
  not not_3 (not_3_out, not_4_out);
  not not_4 (not_4_out, not_2_out);
  D_Flip_Flop d_ff_7 (.clk(not_4_out), .D(d_ff_5_q), .Q(d_ff_7_q), .reset(Button_ON_OFF));  // open: Qn, preset, en
  D_Flip_Flop d_ff_8 (.clk(not_4_out), .D(d_ff_6_q), .Q(d_ff_8_q), .reset(Button_ON_OFF));  // open: Qn, preset, en
  or or_4 (out_14, d_ff_6_q, d_ff_3_q);
  D_Flip_Flop d_ff_9 (.clk(not_3_out), .D(d_ff_8_q), .Q(BZ_end));  // open: Qn, preset, en, reset
  or or_5 (out_13, d_ff_5_q, d_ff_8_q);
  not not_5 (not_5_out, not_3_out);
  D_Flip_Flop d_ff_10 (.clk(not_3_out), .D(d_ff_7_q), .Q(d_ff_10_q), .reset(Button_ON_OFF));  // open: Qn, preset, en
  not not_6 (not_6_out, not_5_out);
  D_Flip_Flop d_ff_11 (.clk(not_5_out), .D(d_ff_10_q), .Q(d_ff_11_q), .reset(Button_ON_OFF));  // open: Qn, preset, en
  D_Flip_Flop d_ff_12 (.clk(not_5_out), .D(BZ_end), .Q(d_ff_12_q));  // open: Qn, preset, en, reset
  not not_7 (not_7_out, not_6_out);
  D_Flip_Flop d_ff_13 (.clk(not_6_out), .D(d_ff_11_q), .Q(d_ff_13_q), .reset(Button_ON_OFF));  // open: Qn, preset, en
  or or_6 (out_12, d_ff_10_q, d_ff_12_q);
  D_Flip_Flop d_ff_14 (.clk(not_7_out), .D(d_ff_13_q), .Q(out_11), .reset(Button_ON_OFF));  // open: Qn, preset, en
  not not_8 (not_8_out, not_7_out);
  D_Flip_Flop d_ff_15 (.clk(not_8_out), .D(out_11), .Q(out_10), .reset(Button_ON_OFF));  // open: Qn, preset, en
  not not_9 (not_9_out, not_8_out);
  D_Flip_Flop d_ff_16 (.clk(not_9_out), .D(out_10), .Q(out_9), .reset(Button_ON_OFF));  // open: Qn, preset, en
endmodule

module PC (
  input  CLK,
  input  in_2,
  input  ON,
  input  in_4,
  input  BZ,
  input  in_6,
  input  in_7,
  input  in_8,
  input  CLK_2,
  input  in_10,
  input  in_11,
  input  Reset,
  output out_13,
  output to_MAR,
  output out_15,
  output out_16
);

  wire ADDER_out_9, ADDER_out_10, ADDER_out_11, ADDER_out_12, d_ff_1_q, or_1_out, or_2_out, or_3_out,
       or_4_out, or_5_out;

  or or_1 (or_1_out, in_7, ADDER_out_12);
  or or_2 (or_2_out, in_4, ADDER_out_9);
  or or_3 (or_3_out, BZ, ADDER_out_10);
  or or_4 (or_4_out, in_6, ADDER_out_11);
  D_Flip_Flop d_ff_1 (.Q(d_ff_1_q), .preset(in_8), .reset(in_11));  // open: clk, D, Qn, en
  or or_5 (or_5_out, in_2, ON);
  register__4_bits PC (
    .in_2(or_2_out), .in_3(or_3_out), .in_4(or_4_out), .in_5(or_1_out), .out_9(out_13), .out_10(to_MAR),
    .out_11(out_15), .out_12(out_16), .in_1(CLK), .Address(CLK_2), .W_R(in_10), .in_6(ON));
  ALU__4_bit ADDER (
    .in_3(out_13), .in_4(to_MAR), .in_5(out_15), .in_6(out_16), .CLK(or_5_out), .CONSTANT(1'b1),
    .out_9(ADDER_out_9), .out_10(ADDER_out_10), .out_11(ADDER_out_11), .out_12(ADDER_out_12),
    .in_8(d_ff_1_q), .BZ(Reset));
endmodule

module BUS_gate (
  input  in_1,
  input  in_2,
  input  in_3,
  input  in_4,
  input  in_5,
  input  in_6,
  input  in_7,
  input  in_8,
  input  in_9,
  input  in_10,
  input  in_11,
  input  in_12,
  input  in_13,
  input  in_14,
  input  in_15,
  input  in_16,
  output out_17,
  output out_18,
  output out_19,
  output out_20,
  output out_21,
  output out_22,
  output out_23,
  output out_24
);

  or or_1 (out_17, in_1, in_2);
  or or_2 (out_18, in_3, in_4);
  or or_3 (out_19, in_5, in_6);
  or or_4 (out_20, in_7, in_8);
  or or_5 (out_21, in_9, in_10);
  or or_6 (out_23, in_13, in_14);
  or or_7 (out_22, in_11, in_12);
  or or_8 (out_24, in_15, in_16);
endmodule

module BUS_CPU_System_gate (
  input  in_1,
  input  in_2,
  input  in_3,
  input  in_4,
  input  in_5,
  input  in_6,
  input  in_7,
  input  in_8,
  input  ON,
  input  in_10,
  output out_11,
  output out_12,
  output out_13,
  output out_14,
  output out_15,
  output out_16,
  output out_17,
  output out_18,
  output out_19,
  output out_20,
  output out_21,
  output out_22,
  output out_23,
  output out_24,
  output out_25,
  output out_26
);

  Demultiplexer demultiplexer_1 (.out0(out_19), .out1(out_11), .in(in_1), .sel(in_10), .en(ON));
  Demultiplexer demultiplexer_2 (.out0(out_20), .out1(out_12), .in(in_2), .sel(in_10), .en(ON));
  Demultiplexer demultiplexer_3 (.out0(out_21), .out1(out_13), .in(in_3), .sel(in_10), .en(ON));
  Demultiplexer demultiplexer_4 (.out0(out_22), .out1(out_14), .in(in_4), .sel(in_10), .en(ON));
  Demultiplexer demultiplexer_5 (.out0(out_23), .out1(out_15), .in(in_5), .sel(in_10), .en(ON));
  Demultiplexer demultiplexer_6 (.out0(out_24), .out1(out_16), .in(in_6), .sel(in_10), .en(ON));
  Demultiplexer demultiplexer_7 (.out0(out_25), .out1(out_17), .in(in_7), .sel(in_10), .en(ON));
  Demultiplexer demultiplexer_8 (.out0(out_26), .out1(out_18), .in(in_8), .sel(in_10), .en(ON));
endmodule

module MAR___MBR (
  input  CU_LD,
  input  in_2,
  input  Reset,
  input  CLK,
  input  in_5,
  input  in_6,
  input  in_7,
  input  in_8,
  input  in_9,
  input  in_10,
  input  in_11,
  input  in_12,
  input  in_13,
  input  in_14,
  input  CLK_2,
  input  Reset_MBR,
  input  in_17,
  input  in_18,
  input  in_19,
  input  in_20,
  input  in_21,
  input  in_22,
  input  in_23,
  input  in_24,
  input  in_25,
  input  in_26,
  output out_27,
  output out_28,
  output out_29,
  output out_30,
  output out_31,
  output out_32,
  output out_33,
  output out_34,
  output out_35,
  output out_36,
  output out_37,
  output out_38
);

  wire multiplexer_1_out, multiplexer_2_out, multiplexer_3_out, multiplexer_4_out, or_1_out, or_2_out,
       or_3_out, or_4_out, or_5_out;

  Multiplexer multiplexer_1 (.in0(in_7), .in1(in_11), .out(multiplexer_1_out), .sel(CU_LD), .en(in_12));
  Multiplexer multiplexer_2 (.in0(in_8), .in1(in_13), .out(multiplexer_2_out), .sel(CU_LD), .en(in_12));
  Multiplexer multiplexer_3 (.in0(in_6), .in1(in_10), .out(multiplexer_3_out), .sel(CU_LD), .en(in_12));
  or or_1 (or_1_out, in_5, in_2);
  Multiplexer multiplexer_4 (.in0(CLK), .in1(in_9), .out(multiplexer_4_out), .sel(CU_LD), .en(in_12));
  or or_2 (or_2_out, Reset, Reset_MBR);
  or or_3 (or_3_out, CLK_2, in_2);
  register__4_bits MAR (
    .in_2(multiplexer_4_out), .in_3(multiplexer_3_out), .in_4(multiplexer_1_out), .in_5(multiplexer_2_out),
    .out_9(out_27), .out_10(out_28), .out_11(out_29), .out_12(out_30), .in_1(or_1_out), .Address(in_12),
    .W_R(or_4_out), .in_6(Reset));
  or or_4 (or_4_out, in_14, CU_LD);
  register__8_bit MBR (
    .in_6(in_17), .in_7(in_18), .in_8(in_19), .in_9(in_20), .in_10(in_21), .in_11(in_22), .in_12(in_23),
    .in_13(in_24), .out_21(out_31), .out_22(out_32), .out_23(out_33), .out_24(out_34), .out_25(out_35),
    .out_26(out_36), .out_27(out_37), .out_28(out_38), .in_1(or_3_out), .W_R(or_5_out), .Address(in_25),
    .RESET(or_2_out));  // open: in_2, in_3, in_4, in_5, in_14, in_15, in_16, in_17
  or or_5 (or_5_out, in_26, CU_LD);
endmodule
